// Logisim project S1-T3 simplified logisim.circ as structural Verilog: 3 circuits, main circuit main
module main (
  input  [1:0] input_HR,
  input  reset
);

  wire and_1_out, comparator_1_eq, comparator_1_gt, comparator_1_lt, comparator_2_gt, monopulse_out,
       n7segdecoder_1_a, n7segdecoder_1_b, n7segdecoder_1_c, n7segdecoder_1_d, n7segdecoder_1_e,
       n7segdecoder_1_f, n7segdecoder_1_g, n7segdecoder_2_a, n7segdecoder_2_b, n7segdecoder_2_c,
       n7segdecoder_2_d, n7segdecoder_2_e, n7segdecoder_2_f, n7segdecoder_2_g;
  wire [1:0] register_2_q, shiftreg_1_output_bit;
  wire [4:0] adder_1_out, bit_extender_1_out, register_1_q;

  Button monopulse (.out(monopulse_out));
  assign bit_extender_1_out = {{3{1'b0}}, input_HR};  // Bit_Extender bit_extender_1
  Comparator #(.width(2), .mode("unsigned")) comparator_1 (
    .a(input_HR), .b(2'b10), .gt(comparator_1_gt), .eq(comparator_1_eq), .lt(comparator_1_lt));
  Adder #(.width(5)) adder_1 (.a(bit_extender_1_out), .b(register_1_q), .out(adder_1_out));  // open: cin, cout
  Register #(.width(5)) register_1 (.D(adder_1_out), .Q(register_1_q), .clk(monopulse_out), .clr(reset));  // open: en
  Comparator #(.width(2), .mode("unsigned")) comparator_2 (
    .a(input_HR), .b(register_2_q), .gt(comparator_2_gt));  // open: eq, lt
  and and_1 (and_1_out, comparator_2_gt, monopulse_out);
  Register #(.width(2)) register_2 (.D(input_HR), .Q(register_2_q), .clk(and_1_out), .clr(reset));  // open: en
  LED GREEN (.in(comparator_1_lt));
  shiftreg shiftreg_1 (.input_bit(register_1_q), .output_bit(shiftreg_1_output_bit));
  LED ORANGE (.in(comparator_1_eq));
  LED RED (.in(comparator_1_gt));
  _7_Segment_Display #(.active("false")) u_7_segment_display_1 (
    .g(n7segdecoder_1_g), .f(n7segdecoder_1_f), .a(n7segdecoder_1_a), .b(n7segdecoder_1_b),
    .e(n7segdecoder_1_e), .d(n7segdecoder_1_d), .c(n7segdecoder_1_c));  // open: dp
  _7segdecoder u_7segdecoder_1 (
    .A1(register_2_q[0]), .A0(register_2_q[1]), .a(n7segdecoder_1_a), .b(n7segdecoder_1_b),
    .c(n7segdecoder_1_c), .d(n7segdecoder_1_d), .e(n7segdecoder_1_e), .f(n7segdecoder_1_f),
    .g(n7segdecoder_1_g));
  _7_Segment_Display #(.active("false")) u_7_segment_display_2 (
    .g(n7segdecoder_2_g), .f(n7segdecoder_2_f), .a(n7segdecoder_2_a), .b(n7segdecoder_2_b),
    .e(n7segdecoder_2_e), .d(n7segdecoder_2_d), .c(n7segdecoder_2_c));  // open: dp
  _7segdecoder u_7segdecoder_2 (
    .A1(shiftreg_1_output_bit[0]), .A0(shiftreg_1_output_bit[1]), .a(n7segdecoder_2_a), .b(n7segdecoder_2_b),
    .c(n7segdecoder_2_c), .d(n7segdecoder_2_d), .e(n7segdecoder_2_e), .f(n7segdecoder_2_f),
    .g(n7segdecoder_2_g));

  // Notes on the sheet:
  //   PEAK HEART RATE
  //   AVERAGE HEART RATE
  //   SIMPLIFIED HARDWARE CIRCUIT DIAGRAM
  //   SAFETY CLASSIFIER
  //   <150 bpm
  //   150-180
  //   bpm
  //   SARTH SHAH 231CS154
  //   ABHIJIT KAR 231CS106
  //   AARYAN YADAV 231CS104
  //   DISPLAY DECODER
  //   MAXIMUM HR
  //   >180 bpm
  //   DISPLAY DECODER
  //   AVERAGE HR
endmodule

module shiftreg (
  input  [4:0] input_bit,
  output [1:0] output_bit
);

  wire [4:0] divider_1_out;

  Divider #(.width(5)) divider_1 (.a(input_bit), .b(5'b00100), .out(divider_1_out));  // open: upper, rem
  Bit_Extender #(.in_width(5), .out_width(2), .\type ("input")) bit_extender_1 (
    .in(divider_1_out), .out(output_bit));  // open: extend
endmodule

module _7segdecoder (
  input  A1,
  input  A0,
  output a,
  output b,
  output c,
  output d,
  output e,
  output f,
  output g
);

  wire decoder_1_out0, decoder_1_out1, decoder_1_out2, decoder_1_out3, decoder_1_out4, decoder_1_out5,
       decoder_1_out6, decoder_1_out7, decoder_1_out9;

  Decoder #(.select(4)) decoder_1 (
    .out0(decoder_1_out0), .out1(decoder_1_out1), .out2(decoder_1_out2), .out3(decoder_1_out3),
    .out4(decoder_1_out4), .out5(decoder_1_out5), .out6(decoder_1_out6), .out7(decoder_1_out7),
    .out9(decoder_1_out9), .sel({2'b00, A1, A0}), .en(1'b1));  // open: out8, out10, out11, out12, out13, out14, out15
  or or_1 (a, decoder_1_out1, decoder_1_out4);
  or or_2 (b, decoder_1_out5, decoder_1_out6);
  or or_3 (c, decoder_1_out2, decoder_1_out2, decoder_1_out2);
  or or_4 (d, decoder_1_out1, decoder_1_out4, decoder_1_out7);
  or or_5 (e, decoder_1_out1, decoder_1_out3, decoder_1_out4, decoder_1_out5, decoder_1_out7, decoder_1_out9);
  or or_6 (f, decoder_1_out1, decoder_1_out2, decoder_1_out3, decoder_1_out7);
  or or_7 (g, decoder_1_out0, decoder_1_out1, decoder_1_out7);
  _7_Segment_Display #(.active("false")) u_7_segment_display_1 (
    .g(g), .f(f), .a(a), .b(b), .e(e), .d(d), .c(c), .dp(1'b1));

  // Notes on the sheet:
  //   a
  //   b
  //   c
  //   d
  //   e
  //   f
  //   g
endmodule
