// Logisim project S1-T3.circ as structural Verilog: 23 circuits, main circuit mod 10 counter
module MAIN (
  input  RESET,
  input  START,
  input  RUN_1,
  input  RUN_2,
  input  RUN_3,
  input  RUN_4,
  input  WALK,
  input  LIGHT_JOG,
  input  RUN,
  input  SPRINT
);

  wire and_1_out, CLOCK_out, display_m_1_a, display_m_1_a1, display_m_1_b, display_m_1_b1, display_m_1_c,
       display_m_1_c1, display_m_1_d, display_m_1_d1, display_m_1_e, display_m_1_e1, display_m_1_f,
       display_m_1_f1, display_m_1_g, display_m_1_g1, display_m_2_a, display_m_2_a1, display_m_2_b,
       display_m_2_b1, display_m_2_c, display_m_2_c1, display_m_2_d, display_m_2_d1, display_m_2_e,
       display_m_2_e1, display_m_2_f, display_m_2_f1, display_m_2_g, display_m_2_g1, display_m_3_a,
       display_m_3_a1, display_m_3_b, display_m_3_b1, display_m_3_c, display_m_3_c1, display_m_3_d,
       display_m_3_d1, display_m_3_e, display_m_3_e1, display_m_3_f, display_m_3_f1, display_m_3_g,
       display_m_3_g1, display_m_4_a, display_m_4_a1, display_m_4_b, display_m_4_b1, display_m_4_c,
       display_m_4_c1, display_m_4_d, display_m_4_d1, display_m_4_e, display_m_4_e1, display_m_4_f,
       display_m_4_f1, display_m_4_g, display_m_4_g1, display_m_5_a, display_m_5_a1, display_m_5_b,
       display_m_5_b1, display_m_5_c, display_m_5_c1, display_m_5_d, display_m_5_d1, display_m_5_e,
       display_m_5_e1, display_m_5_f, display_m_5_f1, display_m_5_g, display_m_5_g1, display_m_6_a,
       display_m_6_a1, display_m_6_b, display_m_6_b1, display_m_6_c, display_m_6_c1, display_m_6_d,
       display_m_6_d1, display_m_6_e, display_m_6_e1, display_m_6_f, display_m_6_f1, display_m_6_g,
       display_m_6_g1, display_x_1_a, display_x_1_a1, display_x_1_b, display_x_1_b1, display_x_1_c,
       display_x_1_c1, display_x_1_d, display_x_1_d1, display_x_1_e, display_x_1_e1, display_x_1_f,
       display_x_1_f1, display_x_1_g, display_x_1_g1, performance_eval_1_win_or_lose;
  wire [3:0] timer_for_lower_display_1_out_3, timer_for_lower_display_1_out_4,
       timer_for_lower_display_1_out_5, timer_for_lower_display_1_out_6, timer_for_lower_display_1_out_7,
       timer_for_lower_display_1_out_8, timer_for_upperr_display_1_out_3, timer_for_upperr_display_1_out_4,
       timer_for_upperr_display_1_out_5, timer_for_upperr_display_1_out_6, timer_for_upperr_display_1_out_7,
       timer_for_upperr_display_1_out_8;
  wire [6:0] classfication1_1_led1, classfication1_1_led2, classfication1_1_led2_2, classification2_1_led1,
       classification2_1_led2, classification2_1_led2_2, performance_eval_1_great,
       performance_eval_1_not_good, performance_eval_1_same, trainer_1_led1, trainer_1_led2, trainer_1_led3;
  wire [11:0] average_calories_1_average, average_calories_1_calories_burnt, hr_generator_1_hr,
       max_hr_1_max_hr, performance_eval_1_laps, speed_distance_1_distnace, speed_distance_1_speed,
       step_generator_1_step_sec, step_generator_1_total_steps, time_elapsed_1_time_seconds;

  Clock CLOCK (.out(CLOCK_out));
  and and_1 (and_1_out, START, CLOCK_out);
  DotMatrix dotmatrix_1 (
    .col0(trainer_1_led1), .col1(trainer_1_led1), .col2(trainer_1_led1), .col3(trainer_1_led1),
    .col4(trainer_1_led1));
  STEP_GENERATOR step_generator_1 (
    .CLR(RESET), .total_steps(step_generator_1_total_steps), .Step_sec(step_generator_1_step_sec));
  _7_Segment_Display #(.active("false")) u_7_segment_display_1 (
    .g(timer_for_upperr_display_1_out_5[3]), .f(timer_for_upperr_display_1_out_5[2]),
    .a(timer_for_upperr_display_1_out_5[1]), .b(timer_for_upperr_display_1_out_5[0]),
    .e(timer_for_lower_display_1_out_5[3]), .d(timer_for_lower_display_1_out_5[2]),
    .c(timer_for_lower_display_1_out_5[1]), .dp(timer_for_lower_display_1_out_5[0]));
  _7_Segment_Display #(.active("false")) u_7_segment_display_2 (
    .g(timer_for_upperr_display_1_out_4[3]), .f(timer_for_upperr_display_1_out_4[2]),
    .a(timer_for_upperr_display_1_out_4[1]), .b(timer_for_upperr_display_1_out_4[0]),
    .e(timer_for_lower_display_1_out_4[3]), .d(timer_for_lower_display_1_out_4[2]),
    .c(timer_for_lower_display_1_out_4[1]), .dp(timer_for_lower_display_1_out_4[0]));
  TRAINER trainer_1 (
    .walk(WALK), .L_jog(LIGHT_JOG), .F_jog(RUN), .Run(SPRINT), .led1(trainer_1_led1), .led2(trainer_1_led2),
    .led3(trainer_1_led3), .STEP_SEC(step_generator_1_step_sec));
  DotMatrix dotmatrix_2 (
    .col0(trainer_1_led2), .col1(trainer_1_led2), .col2(trainer_1_led2), .col3(trainer_1_led2),
    .col4(trainer_1_led2));
  _7_Segment_Display #(.active("false")) u_7_segment_display_3 (
    .g(timer_for_upperr_display_1_out_6[3]), .f(timer_for_upperr_display_1_out_6[2]),
    .a(timer_for_upperr_display_1_out_6[1]), .b(timer_for_upperr_display_1_out_6[0]),
    .e(timer_for_lower_display_1_out_6[3]), .d(timer_for_lower_display_1_out_6[2]),
    .c(timer_for_lower_display_1_out_6[1]), .dp(timer_for_lower_display_1_out_6[0]));
  LED led_1 (.in(performance_eval_1_win_or_lose));
  LED led_2 (.in(performance_eval_1_win_or_lose));
  LED led_3 (.in(performance_eval_1_win_or_lose));
  LED led_4 (.in(performance_eval_1_win_or_lose));
  LED led_5 (.in(performance_eval_1_win_or_lose));
  LED led_6 (.in(performance_eval_1_win_or_lose));
  DotMatrix dotmatrix_3 (
    .col0(trainer_1_led3), .col1(trainer_1_led3), .col2(trainer_1_led3), .col3(trainer_1_led3),
    .col4(trainer_1_led3));
  _7_Segment_Display #(.active("false")) u_7_segment_display_4 (
    .g(timer_for_upperr_display_1_out_7[3]), .f(timer_for_upperr_display_1_out_7[2]),
    .a(timer_for_upperr_display_1_out_7[1]), .b(timer_for_upperr_display_1_out_7[0]),
    .e(timer_for_lower_display_1_out_7[3]), .d(timer_for_lower_display_1_out_7[2]),
    .c(timer_for_lower_display_1_out_7[1]), .dp(timer_for_lower_display_1_out_7[0]));
  LED led_7 (.in(performance_eval_1_win_or_lose));
  LED led_8 (.in(performance_eval_1_win_or_lose));
  LED led_9 (.in(performance_eval_1_win_or_lose));
  LED led_10 (.in(performance_eval_1_win_or_lose));
  LED led_11 (.in(performance_eval_1_win_or_lose));
  LED led_12 (.in(performance_eval_1_win_or_lose));
  LED led_13 (.in(performance_eval_1_win_or_lose));
  _7_Segment_Display #(.active("false")) u_7_segment_display_5 (
    .g(timer_for_upperr_display_1_out_8[3]), .f(timer_for_upperr_display_1_out_8[2]),
    .a(timer_for_upperr_display_1_out_8[1]), .b(timer_for_upperr_display_1_out_8[0]),
    .e(timer_for_lower_display_1_out_8[3]), .d(timer_for_lower_display_1_out_8[2]),
    .c(timer_for_lower_display_1_out_8[1]), .dp(timer_for_lower_display_1_out_8[0]));
  timer_for_upperr_display timer_for_upperr_display_1 (
    .clear(RESET), .clock(and_1_out), .out_4(timer_for_upperr_display_1_out_4),
    .out_5(timer_for_upperr_display_1_out_5), .out_6(timer_for_upperr_display_1_out_6),
    .out_7(timer_for_upperr_display_1_out_7), .out_8(timer_for_upperr_display_1_out_8),
    .out_3(timer_for_upperr_display_1_out_3));
  _7_Segment_Display #(.active("false")) u_7_segment_display_6 (
    .g(timer_for_upperr_display_1_out_3[3]), .f(timer_for_upperr_display_1_out_3[2]),
    .a(timer_for_upperr_display_1_out_3[1]), .b(timer_for_upperr_display_1_out_3[0]),
    .e(timer_for_lower_display_1_out_3[3]), .d(timer_for_lower_display_1_out_3[2]),
    .c(timer_for_lower_display_1_out_3[1]), .dp(timer_for_lower_display_1_out_3[0]));
  timer_for_lower_display timer_for_lower_display_1 (
    .out_4(timer_for_lower_display_1_out_4), .out_5(timer_for_lower_display_1_out_5),
    .out_6(timer_for_lower_display_1_out_6), .out_7(timer_for_lower_display_1_out_7),
    .out_8(timer_for_lower_display_1_out_8), .out_3(timer_for_lower_display_1_out_3), .clear(RESET),
    .clock(and_1_out));
  DotMatrix dotmatrix_4 (
    .col0(performance_eval_1_great), .col1(performance_eval_1_great), .col2(performance_eval_1_great),
    .col3(performance_eval_1_great), .col4(performance_eval_1_great));
  speed___distance speed_distance_1 (
    .distnace(speed_distance_1_distnace), .step_sec(step_generator_1_step_sec),
    .total_step(step_generator_1_total_steps), .speed(speed_distance_1_speed));
  HR_GENERATOR hr_generator_1 (
    .opt1(RUN_1), .opt2(RUN_2), .opt3(RUN_3), .opt4(RUN_4), .CLR(RESET), .HR(hr_generator_1_hr),
    .CLK(and_1_out));
  DotMatrix dotmatrix_5 (
    .col0(performance_eval_1_same), .col1(performance_eval_1_same), .col2(performance_eval_1_same),
    .col3(performance_eval_1_same), .col4(performance_eval_1_same));
  PERFORMANCE_EVAL performance_eval_1 (
    .LAPS(performance_eval_1_laps), .GREAT(performance_eval_1_great), .SAME(performance_eval_1_same),
    .NOT_GOOD(performance_eval_1_not_good), .win_or_lose(performance_eval_1_win_or_lose), .START(START),
    .IN_HR(hr_generator_1_hr));
  DotMatrix dotmatrix_6 (
    .col0(performance_eval_1_not_good), .col1(performance_eval_1_not_good),
    .col2(performance_eval_1_not_good), .col3(performance_eval_1_not_good), .col4(performance_eval_1_not_good));
  DotMatrix dotmatrix_7 (
    .col0(classfication1_1_led1), .col1(classfication1_1_led1), .col2(classfication1_1_led1),
    .col3(classfication1_1_led1), .col4(classfication1_1_led1));
  CLASSFICATION1 classfication1_1 (
    .IN_HR(hr_generator_1_hr), .led1(classfication1_1_led1), .led2(classfication1_1_led2),
    .led2_2(classfication1_1_led2_2));
  DotMatrix dotmatrix_8 (
    .col0(classfication1_1_led2), .col1(classfication1_1_led2), .col2(classfication1_1_led2),
    .col3(classfication1_1_led2), .col4(classfication1_1_led2));
  _7_Segment_Display u_7_segment_display_7 (
    .g(display_m_1_g1), .f(display_m_1_f1), .a(display_m_1_a1), .b(display_m_1_b1), .e(display_m_1_e1),
    .d(display_m_1_d1), .c(display_m_1_c1));  // open: dp
  DotMatrix dotmatrix_9 (
    .col0(classfication1_1_led2_2), .col1(classfication1_1_led2_2), .col2(classfication1_1_led2_2),
    .col3(classfication1_1_led2_2), .col4(classfication1_1_led2_2));
  Max_HR max_hr_1 (.HR(hr_generator_1_hr), .max_hr(max_hr_1_max_hr), .CLR(RESET));
  display_M display_m_1 (
    .a1(display_m_1_a1), .val(hr_generator_1_hr), .b1(display_m_1_b1), .c1(display_m_1_c1),
    .d1(display_m_1_d1), .e1(display_m_1_e1), .g1(display_m_1_g1), .f1(display_m_1_f1), .a(display_m_1_a),
    .b(display_m_1_b), .c(display_m_1_c), .d(display_m_1_d), .e(display_m_1_e), .g(display_m_1_g),
    .f(display_m_1_f));
  _7_Segment_Display u_7_segment_display_8 (
    .g(display_m_1_g), .f(display_m_1_f), .a(display_m_1_a), .b(display_m_1_b), .e(display_m_1_e),
    .d(display_m_1_d), .c(display_m_1_c));  // open: dp
  display_M display_m_2 (
    .a1(display_m_2_a1), .val(speed_distance_1_distnace), .b1(display_m_2_b1), .c1(display_m_2_c1),
    .d1(display_m_2_d1), .e1(display_m_2_e1), .g1(display_m_2_g1), .f1(display_m_2_f1), .a(display_m_2_a),
    .b(display_m_2_b), .c(display_m_2_c), .d(display_m_2_d), .e(display_m_2_e), .g(display_m_2_g),
    .f(display_m_2_f));
  _7_Segment_Display u_7_segment_display_9 (
    .g(display_m_2_g1), .f(display_m_2_f1), .a(display_m_2_a1), .b(display_m_2_b1), .e(display_m_2_e1),
    .d(display_m_2_d1), .c(display_m_2_c1));  // open: dp
  _7_Segment_Display u_7_segment_display_10 (
    .g(display_m_2_g), .f(display_m_2_f), .a(display_m_2_a), .b(display_m_2_b), .e(display_m_2_e),
    .d(display_m_2_d), .c(display_m_2_c));  // open: dp
  AVERAGE___CALORIES average_calories_1 (
    .RESET(RESET), .IN_AVG(hr_generator_1_hr), .AVERAGE(average_calories_1_average),
    .CALORIES_BURNT(average_calories_1_calories_burnt), .TIME(time_elapsed_1_time_seconds));
  time_elapsed time_elapsed_1 (.clr(RESET), .TIME_SECONDS(time_elapsed_1_time_seconds));
  display_M display_m_3 (
    .a1(display_m_3_a1), .val(max_hr_1_max_hr), .b1(display_m_3_b1), .c1(display_m_3_c1),
    .d1(display_m_3_d1), .e1(display_m_3_e1), .g1(display_m_3_g1), .f1(display_m_3_f1), .a(display_m_3_a),
    .b(display_m_3_b), .c(display_m_3_c), .d(display_m_3_d), .e(display_m_3_e), .g(display_m_3_g),
    .f(display_m_3_f));
  _7_Segment_Display u_7_segment_display_11 (
    .g(display_m_3_g), .f(display_m_3_f), .a(display_m_3_a), .b(display_m_3_b), .e(display_m_3_e),
    .d(display_m_3_d), .c(display_m_3_c));  // open: dp
  _7_Segment_Display u_7_segment_display_12 (
    .g(display_m_3_g1), .f(display_m_3_f1), .a(display_m_3_a1), .b(display_m_3_b1), .e(display_m_3_e1),
    .d(display_m_3_d1), .c(display_m_3_c1));  // open: dp
  display_M display_m_4 (
    .a1(display_m_4_a1), .val(speed_distance_1_speed), .b1(display_m_4_b1), .c1(display_m_4_c1),
    .d1(display_m_4_d1), .e1(display_m_4_e1), .g1(display_m_4_g1), .f1(display_m_4_f1), .a(display_m_4_a),
    .b(display_m_4_b), .c(display_m_4_c), .d(display_m_4_d), .e(display_m_4_e), .g(display_m_4_g),
    .f(display_m_4_f));
  _7_Segment_Display u_7_segment_display_13 (
    .g(display_m_4_g1), .f(display_m_4_f1), .a(display_m_4_a1), .b(display_m_4_b1), .e(display_m_4_e1),
    .d(display_m_4_d1), .c(display_m_4_c1));  // open: dp
  _7_Segment_Display u_7_segment_display_14 (
    .g(display_m_4_g), .f(display_m_4_f), .a(display_m_4_a), .b(display_m_4_b), .e(display_m_4_e),
    .d(display_m_4_d), .c(display_m_4_c));  // open: dp
  display_M display_m_5 (
    .a1(display_m_5_a1), .val(average_calories_1_calories_burnt), .b1(display_m_5_b1), .c1(display_m_5_c1),
    .d1(display_m_5_d1), .e1(display_m_5_e1), .g1(display_m_5_g1), .f1(display_m_5_f1), .a(display_m_5_a),
    .b(display_m_5_b), .c(display_m_5_c), .d(display_m_5_d), .e(display_m_5_e), .g(display_m_5_g),
    .f(display_m_5_f));
  _7_Segment_Display u_7_segment_display_15 (
    .g(display_m_5_g1), .f(display_m_5_f1), .a(display_m_5_a1), .b(display_m_5_b1), .e(display_m_5_e1),
    .d(display_m_5_d1), .c(display_m_5_c1));  // open: dp
  _7_Segment_Display u_7_segment_display_16 (
    .g(display_x_1_g1), .f(display_x_1_f1), .a(display_x_1_a1), .b(display_x_1_b1), .e(display_x_1_c1),
    .d(display_x_1_d1), .c(display_x_1_e1));  // open: dp
  DotMatrix dotmatrix_10 (
    .col0(classification2_1_led1), .col1(classification2_1_led1), .col2(classification2_1_led1),
    .col3(classification2_1_led1), .col4(classification2_1_led1));
  _7_Segment_Display u_7_segment_display_17 (
    .g(display_m_5_g), .f(display_m_5_f), .a(display_m_5_a), .b(display_m_5_b), .e(display_m_5_e),
    .d(display_m_5_d), .c(display_m_5_c));  // open: dp
  display_X display_x_1 (
    .val(performance_eval_1_laps), .a1(display_x_1_a1), .b1(display_x_1_b1), .c1(display_x_1_c1),
    .d1(display_x_1_d1), .e1(display_x_1_e1), .g1(display_x_1_g1), .f1(display_x_1_f1), .a(display_x_1_a),
    .b(display_x_1_b), .c(display_x_1_c), .d(display_x_1_d), .e(display_x_1_e), .g(display_x_1_g),
    .f(display_x_1_f));
  _7_Segment_Display u_7_segment_display_18 (
    .g(display_x_1_g), .f(display_x_1_f), .a(display_x_1_a), .b(display_x_1_b), .e(display_x_1_e),
    .d(display_x_1_d), .c(display_x_1_c));  // open: dp
  CLASSIFICATION2 classification2_1 (
    .IN_HR(average_calories_1_average), .led1(classification2_1_led1), .led2(classification2_1_led2),
    .led2_2(classification2_1_led2_2));
  DotMatrix dotmatrix_11 (
    .col0(classification2_1_led2), .col1(classification2_1_led2), .col2(classification2_1_led2),
    .col3(classification2_1_led2), .col4(classification2_1_led2));
  _7_Segment_Display u_7_segment_display_19 (
    .g(display_m_6_g1), .f(display_m_6_f1), .a(display_m_6_a1), .b(display_m_6_b1), .e(display_m_6_e1),
    .d(display_m_6_d1), .c(display_m_6_c1));  // open: dp
  display_M display_m_6 (
    .a1(display_m_6_a1), .val(average_calories_1_average), .b1(display_m_6_b1), .c1(display_m_6_c1),
    .d1(display_m_6_d1), .e1(display_m_6_e1), .g1(display_m_6_g1), .f1(display_m_6_f1), .a(display_m_6_a),
    .b(display_m_6_b), .c(display_m_6_c), .d(display_m_6_d), .e(display_m_6_e), .g(display_m_6_g),
    .f(display_m_6_f));
  _7_Segment_Display u_7_segment_display_20 (
    .g(display_m_6_g), .f(display_m_6_f), .a(display_m_6_a), .b(display_m_6_b), .e(display_m_6_e),
    .d(display_m_6_d), .c(display_m_6_c));  // open: dp
  DotMatrix dotmatrix_12 (
    .col0(classification2_1_led2_2), .col1(classification2_1_led2_2), .col2(classification2_1_led2_2),
    .col3(classification2_1_led2_2), .col4(classification2_1_led2_2));

  // Notes on the sheet:
  //   on -->
  //   RANGE OF HR VALUES
  //   81-144 bpm -------->
  //   100 -170 bpm------->
  //   121 -198 bpm------->
  //   96 -152 bpm------->
  //   EXPECTED STEP/SEC  VALUE
  //   1 step/sec----->
  //   2 step/sec----->
  //   3 step/sec----->
  //   4 step/sec----->
  //   REDUCE SPEED
  //   PEDOMETER
  //   GOOD JOB
  //   (PERFOMANCE BETTER THAN PREVIOUS TIME )
  //   iNCREASE SPEED
  //   RUNNERS PERFOMANCE MONITORING SYSTEM
  //   TEAM ID - S1-T3
  //   SARTH SHAH , 231CS154
  //   ABHIJIT KAR , 231CS106
  //   AARYAN YADAV,231CS104
  //   VICTORY!!!
  //   DOING BETTER!
  //   KEEP IT UP
  //   HEART RATE MONITORING SYSTEM
  //   SAME PROGRESS
  //   SAFE ZONE
  //   WARNING 
  //   ZONE
  //   IMPROVE IT !
  //   DANGER ZONE 
  //   CURRENT HR
  //   (BPM/2)
  //   DISTANCE(M)
  //   PEAK HR
  //   (BPM2)
  //   SPEED 
  //   (M/S)
  //   1.TURN  ON THE START BUTTON 
  //   2. SELECT A RUN (4 OPTIONS )
  //   <110 BPM
  //   CALORIES BURNT
  //   (KCAL)
  //   3.SELECT THE TYPE OF RUN (4 OPTIONS)
  //   WARM UP ZONE 
  //   NUMBER OF LAPS 
  //   4. ENABLE THE CLOCKING AND CIRCUIT WILL START
  //   AVERAGE HR
  //   (BPM/2)
  //   5.CIRCUIT WILL DISPLAY LIVE CLASSFICATIONS AND PARAMETERS OF THE RUN 
  //   110-160 BPM
  //   CARDIO ZONE 
  //   INSTRUCTIONS TO USE 
  //   6. ONCE THE RUN IS DONE, TURN OFF THE START BUTTON & FINAL RESULTS DISPLAYED
  //   >160 BPM
  //   EXTREME
  //   ZONE
  //   (INPUTS AT TOP LEFT)
  //   (OUTPUTS AT BOTTOM RIGHT)
endmodule

module HR_GENERATOR (
  input  CLK,
  input  CLR,
  input  opt1,
  input  opt2,
  input  opt3,
  input  opt4,
  output [11:0] HR
);

  wire and_1_out, and_2_out, and_3_out, and_4_out, and_5_out, and_6_out, j_k_ff_1_q, j_k_ff_2_q, j_k_ff_3_q,
       j_k_ff_4_q, not_1_out, not_2_out, not_3_out, not_4_out, not_5_out, not_6_out;
  wire [1:0] priority_encoder_1_out;
  wire [2:0] or_1_out;
  wire [3:0] multiplexer_1_out;
  wire [7:0] adder_1_out, bit_extender_1_out, bit_extender_2_out, multiplexer_2_out, multiplier_1_out;

  not not_1 (not_1_out, j_k_ff_4_q);
  not not_2 (not_2_out, j_k_ff_1_q);
  and and_1 (and_1_out, j_k_ff_4_q, not_2_out);
  or or_1 (or_1_out[0], and_1_out, and_3_out);
  Priority_Encoder #(.select(2)) priority_encoder_1 (
    .in0(opt1), .in1(opt2), .in2(opt3), .in3(opt4), .out(priority_encoder_1_out));  // open: gs, en_out, en_in
  J_K_Flip_Flop #(.trigger("falling")) j_k_ff_1 (
    .J(1'b1), .clk(CLK), .K(1'b1), .Q(j_k_ff_1_q), .reset(CLR));  // open: Qn, preset, en
  not not_3 (not_3_out, j_k_ff_2_q);
  and and_2 (and_2_out, not_3_out, j_k_ff_4_q);
  and and_3 (and_3_out, not_1_out, j_k_ff_1_q);
  Multiplexer #(.select(2), .width(4)) multiplexer_1 (
    .in0(4'b1001), .in1(4'b1010), .in2(4'b1011), .in3(4'b1100), .out(multiplexer_1_out),
    .sel(priority_encoder_1_out));  // open: en
  J_K_Flip_Flop #(.trigger("falling")) j_k_ff_2 (
    .J(1'b1), .clk(j_k_ff_1_q), .K(1'b1), .Q(j_k_ff_2_q), .reset(CLR));  // open: Qn, preset, en
  not not_4 (not_4_out, j_k_ff_4_q);
  and and_4 (and_4_out, j_k_ff_2_q, not_4_out);
  or or_2 (or_1_out[1], and_2_out, and_4_out);
  J_K_Flip_Flop #(.trigger("falling")) j_k_ff_3 (
    .J(1'b1), .clk(j_k_ff_2_q), .K(1'b1), .Q(j_k_ff_3_q), .reset(CLR));  // open: Qn, preset, en
  not not_5 (not_5_out, j_k_ff_3_q);
  and and_5 (and_5_out, not_5_out, j_k_ff_4_q);
  assign bit_extender_1_out = {{5{1'b0}}, or_1_out};  // Bit_Extender bit_extender_1
  assign bit_extender_2_out = {{4{1'b0}}, multiplexer_1_out};  // Bit_Extender bit_extender_2
  Multiplexer #(.select(2), .width(8)) multiplexer_2 (
    .in0(8'h9), .in1(8'ha), .in2(8'hb), .in3(8'h8), .out(multiplexer_2_out), .sel(priority_encoder_1_out));  // open: en
  J_K_Flip_Flop #(.trigger("falling")) j_k_ff_4 (
    .J(1'b1), .clk(j_k_ff_3_q), .K(1'b1), .Q(j_k_ff_4_q), .reset(CLR));  // open: Qn, preset, en
  and and_6 (and_6_out, j_k_ff_3_q, not_6_out);
  or or_3 (or_1_out[2], and_5_out, and_6_out);
  Adder adder_1 (.a(bit_extender_1_out), .b(bit_extender_2_out), .out(adder_1_out));  // open: cin, cout
  not not_6 (not_6_out, j_k_ff_4_q);
  Multiplier multiplier_1 (.a(adder_1_out), .b(multiplexer_2_out), .out(multiplier_1_out));  // open: cin, cout
  assign HR = {{4{1'b0}}, multiplier_1_out};  // Bit_Extender bit_extender_3

  // Notes on the sheet:
  //   HEART RATE GENERATOR - generates new heart rate values in a range every second
endmodule

module PERFORMANCE_EVAL (
  input  START,
  input  [11:0] IN_HR,
  output [6:0] GREAT,
  output [6:0] SAME,
  output [6:0] NOT_GOOD,
  output win_or_lose,
  output [11:0] LAPS
);

  wire clock_1_out, clock_2_out, clock_3_out, clock_4_out, comparator_1_eq, comparator_1_gt, comparator_1_lt,
       comparator_2_gt, not_1_out, or_1_out, or_2_out, or_3_out, or_4_out, or_5_out, or_6_out, or_7_out,
       or_8_out, or_9_out, or_10_out, or_11_out, or_12_out, or_13_out, or_14_out, or_15_out, or_16_out,
       or_17_out, t_ff_1_qn, t_ff_2_q;
  wire [3:0] counter_1_q;
  wire [7:0] _0_q, _1_q, _2_q, _3_q, _4_q, _5_q, _6_q, _7_q, _8_q, _9_q, _10_q, _11_q, _12_q, _13_q, _14_q,
       bit_extender_1_out, counter_3_q, counter_4_q, demultiplexer_1_out0, demultiplexer_1_out1,
       demultiplexer_1_out2, demultiplexer_1_out3, demultiplexer_1_out4, demultiplexer_1_out5,
       demultiplexer_1_out6, demultiplexer_1_out7, demultiplexer_1_out8, demultiplexer_1_out9,
       demultiplexer_1_out10, demultiplexer_1_out11, demultiplexer_1_out12, demultiplexer_1_out13,
       demultiplexer_1_out14, demultiplexer_1_out15, multiplexer_1_out;

  Clock #(.highDuration(4), .lowDuration(4)) clock_1 (.out(clock_1_out));
  Bit_Extender #(.in_width(12), .out_width(8)) bit_extender_1 (.in(IN_HR), .out(bit_extender_1_out));
  Counter #(.width(4), .max('hf), .trigger("falling")) counter_1 (
    .count(1'b1), .Q(counter_1_q), .clk(clock_1_out), .clr(or_1_out));  // open: load, D, carry
  not not_1 (not_1_out, START);
  Demultiplexer #(.select(4), .width(8)) demultiplexer_1 (
    .out0(demultiplexer_1_out0), .out1(demultiplexer_1_out1), .out2(demultiplexer_1_out2),
    .out3(demultiplexer_1_out3), .out4(demultiplexer_1_out4), .out5(demultiplexer_1_out5),
    .out6(demultiplexer_1_out6), .out7(demultiplexer_1_out7), .out8(demultiplexer_1_out8),
    .out9(demultiplexer_1_out9), .out10(demultiplexer_1_out10), .out11(demultiplexer_1_out11),
    .out12(demultiplexer_1_out12), .out13(demultiplexer_1_out13), .out14(demultiplexer_1_out14),
    .out15(demultiplexer_1_out15), .in(bit_extender_1_out), .sel(counter_1_q));  // open: en
  or or_1 (or_1_out, not_1_out, or_3_out);
  Register #(.trigger("falling")) _0 (.D(bit_extender_1_out), .Q(_0_q), .clk(or_2_out));  // open: en, clr
  or or_2 (or_2_out, demultiplexer_1_out0[0], demultiplexer_1_out0[1], demultiplexer_1_out0[2], demultiplexer_1_out0[3], demultiplexer_1_out0[5], demultiplexer_1_out0[6], demultiplexer_1_out0[7]);
  or or_3 (or_3_out, demultiplexer_1_out15[0], demultiplexer_1_out15[1], demultiplexer_1_out15[2], demultiplexer_1_out15[3], demultiplexer_1_out15[5], demultiplexer_1_out15[6], demultiplexer_1_out15[7]);
  Counter #(.width(12), .max('hfff)) counter_2 (.count(1'b1), .Q(LAPS), .clk(or_3_out));  // open: load, D, carry, clr
  Register #(.trigger("falling")) _1 (.D(bit_extender_1_out), .Q(_1_q), .clk(or_4_out));  // open: en, clr
  or or_4 (or_4_out, demultiplexer_1_out1[0], demultiplexer_1_out1[1], demultiplexer_1_out1[2], demultiplexer_1_out1[3], demultiplexer_1_out1[5], demultiplexer_1_out1[6], demultiplexer_1_out1[7]);
  or or_5 (or_5_out, demultiplexer_1_out14[0], demultiplexer_1_out14[1], demultiplexer_1_out14[2], demultiplexer_1_out14[3], demultiplexer_1_out14[5], demultiplexer_1_out14[6], demultiplexer_1_out14[7]);
  Register #(.trigger("falling")) _14 (.D(bit_extender_1_out), .Q(_14_q), .clk(or_5_out));  // open: en, clr
  Register #(.trigger("falling")) _2 (.D(bit_extender_1_out), .Q(_2_q), .clk(or_6_out));  // open: en, clr
  or or_6 (or_6_out, demultiplexer_1_out2[0], demultiplexer_1_out2[1], demultiplexer_1_out2[2], demultiplexer_1_out2[3], demultiplexer_1_out2[5], demultiplexer_1_out2[6], demultiplexer_1_out2[7]);
  or or_7 (or_7_out, demultiplexer_1_out13[0], demultiplexer_1_out13[1], demultiplexer_1_out13[2], demultiplexer_1_out13[3], demultiplexer_1_out13[5], demultiplexer_1_out13[6], demultiplexer_1_out13[7]);
  Register #(.trigger("falling")) _13 (.D(bit_extender_1_out), .Q(_13_q), .clk(or_7_out));  // open: en, clr
  Register #(.trigger("falling")) _3 (.D(bit_extender_1_out), .Q(_3_q), .clk(or_8_out));  // open: en, clr
  or or_8 (or_8_out, demultiplexer_1_out3[0], demultiplexer_1_out3[1], demultiplexer_1_out3[2], demultiplexer_1_out3[3], demultiplexer_1_out3[5], demultiplexer_1_out3[6], demultiplexer_1_out3[7]);
  or or_9 (or_9_out, demultiplexer_1_out12[0], demultiplexer_1_out12[1], demultiplexer_1_out12[2], demultiplexer_1_out12[3], demultiplexer_1_out12[5], demultiplexer_1_out12[6], demultiplexer_1_out12[7]);
  Register #(.trigger("falling")) _12 (.D(bit_extender_1_out), .Q(_12_q), .clk(or_9_out));  // open: en, clr
  Register #(.trigger("falling")) _4 (.D(bit_extender_1_out), .Q(_4_q), .clk(or_10_out));  // open: en, clr
  or or_10 (or_10_out, demultiplexer_1_out4[0], demultiplexer_1_out4[1], demultiplexer_1_out4[2], demultiplexer_1_out4[3], demultiplexer_1_out4[5], demultiplexer_1_out4[6], demultiplexer_1_out4[7]);
  or or_11 (or_11_out, demultiplexer_1_out11[0], demultiplexer_1_out11[1], demultiplexer_1_out11[2], demultiplexer_1_out11[3], demultiplexer_1_out11[5], demultiplexer_1_out11[6], demultiplexer_1_out11[7]);
  Register #(.trigger("falling")) _11 (.D(bit_extender_1_out), .Q(_11_q), .clk(or_11_out));  // open: en, clr
  Register #(.trigger("falling")) _5 (.D(bit_extender_1_out), .Q(_5_q), .clk(or_12_out));  // open: en, clr
  or or_12 (or_12_out, demultiplexer_1_out5[0], demultiplexer_1_out5[1], demultiplexer_1_out5[2], demultiplexer_1_out5[3], demultiplexer_1_out5[5], demultiplexer_1_out5[6], demultiplexer_1_out5[7]);
  or or_13 (or_13_out, demultiplexer_1_out10[0], demultiplexer_1_out10[1], demultiplexer_1_out10[2], demultiplexer_1_out10[3], demultiplexer_1_out10[5], demultiplexer_1_out10[6], demultiplexer_1_out10[7]);
  Register #(.trigger("falling")) _10 (.D(bit_extender_1_out), .Q(_10_q), .clk(or_13_out));  // open: en, clr
  Register #(.trigger("falling")) _6 (.D(bit_extender_1_out), .Q(_6_q), .clk(or_14_out));  // open: en, clr
  or or_14 (or_14_out, demultiplexer_1_out6[0], demultiplexer_1_out6[1], demultiplexer_1_out6[2], demultiplexer_1_out6[3], demultiplexer_1_out6[5], demultiplexer_1_out6[6], demultiplexer_1_out6[7]);
  or or_15 (or_15_out, demultiplexer_1_out9[0], demultiplexer_1_out9[1], demultiplexer_1_out9[2], demultiplexer_1_out9[3], demultiplexer_1_out9[5], demultiplexer_1_out9[6], demultiplexer_1_out9[7]);
  Register #(.trigger("falling")) _9 (.D(bit_extender_1_out), .Q(_9_q), .clk(or_15_out));  // open: en, clr
  Register #(.trigger("falling")) _7 (.D(bit_extender_1_out), .Q(_7_q), .clk(or_16_out));  // open: en, clr
  or or_16 (or_16_out, demultiplexer_1_out7[0], demultiplexer_1_out7[1], demultiplexer_1_out7[2], demultiplexer_1_out7[3], demultiplexer_1_out7[5], demultiplexer_1_out7[6], demultiplexer_1_out7[7]);
  or or_17 (or_17_out, demultiplexer_1_out8[0], demultiplexer_1_out8[1], demultiplexer_1_out8[2], demultiplexer_1_out8[3], demultiplexer_1_out8[5], demultiplexer_1_out8[6], demultiplexer_1_out8[7]);
  Register #(.trigger("falling")) _8 (.D(bit_extender_1_out), .Q(_8_q), .clk(or_17_out));  // open: en, clr
  Multiplexer #(.select(4), .width(8)) multiplexer_1 (
    .in0(_0_q), .in1(_1_q), .in2(_2_q), .in3(_3_q), .in4(_4_q), .in5(_5_q), .in6(_6_q), .in7(_7_q),
    .in8(_8_q), .in9(_9_q), .in10(_10_q), .in11(_11_q), .in12(_12_q), .in13(_13_q), .in14(_14_q),
    .out(multiplexer_1_out), .sel(counter_1_q));  // open: in15, en
  Comparator #(.mode("unsigned")) comparator_1 (
    .a(bit_extender_1_out), .b(multiplexer_1_out), .gt(comparator_1_gt), .eq(comparator_1_eq),
    .lt(comparator_1_lt));
  Clock clock_2 (.out(clock_2_out));
  Multiplexer #(.width(7)) multiplexer_2 (
    .in0({7{1'b0}}), .in1({7{1'b1}}), .out(GREAT), .sel(comparator_1_gt));  // open: en
  Multiplexer #(.width(7)) multiplexer_3 (
    .in0({7{1'b0}}), .in1({7{1'b1}}), .out(SAME), .sel(comparator_1_eq));  // open: en
  Multiplexer #(.width(7)) multiplexer_4 (
    .in0({7{1'b0}}), .in1({7{1'b1}}), .out(NOT_GOOD), .sel(comparator_1_lt));  // open: en
  T_Flip_Flop t_ff_1 (.clk(clock_2_out), .T(comparator_1_gt), .Qn(t_ff_1_qn));  // open: Q, preset, reset, en
  Clock clock_3 (.out(clock_3_out));
  T_Flip_Flop t_ff_2 (.clk(clock_3_out), .T(comparator_1_lt), .Q(t_ff_2_q));  // open: Qn, preset, reset, en
  Counter counter_3 (.count(1'b1), .Q(counter_3_q), .clk(t_ff_1_qn), .clr(or_1_out));  // open: load, D, carry
  Counter counter_4 (.count(1'b1), .Q(counter_4_q), .clk(t_ff_2_q), .clr(or_1_out));  // open: load, D, carry
  Comparator #(.mode("unsigned")) comparator_2 (
    .a(counter_3_q), .b(counter_4_q), .gt(comparator_2_gt));  // open: eq, lt
  Clock clock_4 (.out(clock_4_out));
  T_Flip_Flop t_ff_3 (.clk(clock_4_out), .T(comparator_2_gt), .Q(win_or_lose));  // open: Qn, preset, reset, en

  // Notes on the sheet:
  //   -> provides conclusion at the end of each run
  //   FUNCTION ->  a memory storing part which stores the data of the previous run of the athelete
  //   PERFORMANCE EVALUATOR 
  //   -> compares the data of current run with the stored data, and once run is completed, updates the new data 
endmodule

module AVERAGE___CALORIES (
  input  RESET,
  input  [11:0] IN_AVG,
  input  [11:0] TIME,
  output [11:0] CALORIES_BURNT,
  output [11:0] AVERAGE
);

  wire and_1_out, clock_1_out;
  wire [11:0] multiplexer_1_out;
  wire [15:0] adder_1_out, bit_extender_1_out, bit_extender_2_out, counter_1_q, COUNTER_2_q, divider_1_out,
       divider_2_out, multiplier_1_out, multiplier_2_out, REGISTER_q, subtractor_1_out;

  Multiplexer #(.width(12)) multiplexer_1 (
    .in0(IN_AVG), .in1({12{1'b0}}), .out(multiplexer_1_out), .sel(RESET));  // open: en
  Clock clock_1 (.out(clock_1_out));
  and and_1 (and_1_out, RESET, clock_1_out);
  assign bit_extender_1_out = {{4{1'b0}}, multiplexer_1_out};  // Bit_Extender bit_extender_1
  Counter #(.width(16), .max('hffff)) counter_1 (
    .Q(counter_1_q), .clk(clock_1_out), .clr(and_1_out));  // open: load, D, count, carry
  Divider #(.width(16)) divider_1 (.a(adder_1_out), .b(counter_1_q), .out(divider_1_out));  // open: upper, rem
  Adder #(.width(16)) adder_1 (.a(COUNTER_2_q), .b(multiplier_1_out), .out(adder_1_out));  // open: cin, cout
  Counter #(.width(16), .max('hffff)) COUNTER_2 (
    .load(1'b1), .D(bit_extender_1_out), .count(1'b0), .Q(COUNTER_2_q), .clk(clock_1_out), .clr(1'b0));  // open: carry
  Subtractor #(.width(16)) subtractor_1 (.a(counter_1_q), .b(16'h1), .out(subtractor_1_out));  // open: bin, bout
  Multiplier #(.width(16)) multiplier_1 (
    .a(subtractor_1_out), .b(REGISTER_q), .out(multiplier_1_out));  // open: cin, cout
  Register #(.width(16)) REGISTER (.D(divider_1_out), .Q(REGISTER_q), .clk(clock_1_out), .clr(and_1_out));  // open: en
  assign bit_extender_2_out = {{4{1'b0}}, TIME};  // Bit_Extender bit_extender_2
  Bit_Extender #(.in_width(16), .out_width(12)) bit_extender_3 (.in(divider_1_out), .out(AVERAGE));
  Multiplier #(.width(16)) multiplier_2 (
    .a(bit_extender_2_out), .b(divider_1_out), .out(multiplier_2_out));  // open: cin, cout
  Divider #(.width(16)) divider_2 (.a(multiplier_2_out), .b(16'h14d), .out(divider_2_out));  // open: upper, rem
  Bit_Extender #(.in_width(16), .out_width(12)) bit_extender_4 (.in(divider_2_out), .out(CALORIES_BURNT));

  // Notes on the sheet:
  //   COUNTER
  //   AVERAGE  HEART RATE AND CALORIES BURNT CALCULATOR 
  //   ADDER
  //   DIVIDER
  //   a series of combinational logic used to calculate important parameters like average HR and calories
  //   SUBTRACTOR
  //   MULTIPLIER
endmodule

module Max_HR (
  input  [11:0] HR,
  input  CLR,
  output [11:0] max_hr
);

  wire clock_1_out, comparator_1_gt, t_ff_1_q;

  Clock clock_1 (.out(clock_1_out));
  Comparator #(.width(12), .mode("unsigned")) comparator_1 (.a(HR), .b(max_hr), .gt(comparator_1_gt));  // open: eq, lt
  T_Flip_Flop t_ff_1 (.clk(clock_1_out), .T(comparator_1_gt), .Q(t_ff_1_q), .reset(CLR));  // open: Qn, preset, en
  Register #(.width(12)) register_1 (.D(HR), .Q(max_hr), .clk(t_ff_1_q), .clr(CLR));  // open: en

  // Notes on the sheet:
  //   PEAK HEART RATE 
endmodule

module STEP_GENERATOR (
  input  CLR,
  output [11:0] total_steps,
  output [11:0] Step_sec
);

  wire and_1_out, and_2_out, and_3_out, and_4_out, clock_1_out, j_k_ff_1_q, j_k_ff_2_q, j_k_ff_3_q,
       not_1_out, not_2_out, not_3_out, not_4_out, not_5_out;
  wire [1:0] or_2_out;
  wire [2:0] adder_2_out, bit_extender_2_out;
  wire [11:0] adder_1_out;

  Clock clock_1 (.out(clock_1_out));
  J_K_Flip_Flop #(.trigger("falling")) j_k_ff_1 (
    .J(1'b1), .clk(clock_1_out), .K(1'b1), .Q(j_k_ff_1_q), .reset(CLR));  // open: Qn, preset, en
  Adder #(.width(12)) adder_1 (.a(total_steps), .b(Step_sec), .out(adder_1_out));  // open: cin, cout
  not not_1 (not_1_out, clock_1_out);
  J_K_Flip_Flop #(.trigger("falling")) j_k_ff_2 (
    .J(1'b1), .clk(j_k_ff_1_q), .K(1'b1), .Q(j_k_ff_2_q), .reset(CLR));  // open: Qn, preset, en
  Register #(.width(12)) register_1 (.D(adder_1_out), .Q(total_steps), .clk(not_1_out));  // open: en, clr
  assign Step_sec = {{9{1'b0}}, adder_2_out};  // Bit_Extender bit_extender_1
  J_K_Flip_Flop #(.trigger("falling")) j_k_ff_3 (
    .J(1'b1), .clk(j_k_ff_2_q), .K(1'b1), .Q(j_k_ff_3_q), .reset(CLR));  // open: Qn, preset, en
  not not_2 (not_2_out, j_k_ff_3_q);
  not not_3 (not_3_out, j_k_ff_2_q);
  not not_4 (not_4_out, j_k_ff_3_q);
  not not_5 (not_5_out, j_k_ff_1_q);
  Adder #(.width(3)) adder_2 (.a(bit_extender_2_out), .b(3'b001), .out(adder_2_out));  // open: cin, cout
  and and_1 (and_1_out, not_2_out, j_k_ff_2_q);
  and and_2 (and_2_out, j_k_ff_3_q, not_3_out);
  and and_3 (and_3_out, not_4_out, j_k_ff_1_q);
  and and_4 (and_4_out, j_k_ff_3_q, not_5_out);
  assign bit_extender_2_out = {{1{1'b0}}, or_2_out};  // Bit_Extender bit_extender_2
  or or_1 (or_2_out[1], and_1_out, and_2_out);
  or or_2 (or_2_out[0], and_3_out, and_4_out);

  // Notes on the sheet:
  //   STEP GENERATOR 
  //   generates new values of step/sec in regular interval
endmodule

module TRAINER (
  input  [11:0] STEP_SEC,
  input  walk,
  input  L_jog,
  input  F_jog,
  input  Run,
  output [6:0] led1,
  output [6:0] led2,
  output [6:0] led3
);

  wire comparator_1_eq, comparator_1_gt, comparator_1_lt;
  wire [1:0] priority_encoder_1_out;
  wire [3:0] bit_extender_1_out, multiplexer_1_out;

  Bit_Extender #(.in_width(12), .out_width(4)) bit_extender_1 (.in(STEP_SEC), .out(bit_extender_1_out));
  Multiplexer #(.select(2), .width(4)) multiplexer_1 (
    .in0(4'b0001), .in1(4'b0010), .in2(4'b0011), .in3(4'b0100), .out(multiplexer_1_out),
    .sel(priority_encoder_1_out));  // open: en
  Priority_Encoder #(.select(2)) priority_encoder_1 (
    .in0(walk), .in1(L_jog), .in2(F_jog), .in3(Run), .out(priority_encoder_1_out));  // open: gs, en_out, en_in
  Comparator #(.width(4), .mode("unsigned")) comparator_1 (
    .a(bit_extender_1_out), .b(multiplexer_1_out), .gt(comparator_1_gt), .eq(comparator_1_eq),
    .lt(comparator_1_lt));
  Multiplexer #(.width(7)) multiplexer_2 (
    .in0({7{1'b0}}), .in1({7{1'b1}}), .out(led1), .sel(comparator_1_gt));  // open: en
  Multiplexer #(.width(7)) multiplexer_3 (
    .in0({7{1'b0}}), .in1({7{1'b1}}), .out(led2), .sel(comparator_1_eq));  // open: en
  Multiplexer #(.width(7)) multiplexer_4 (
    .in0({7{1'b0}}), .in1({7{1'b1}}), .out(led3), .sel(comparator_1_lt));  // open: en

  // Notes on the sheet:
  //   TRAINER MODULE 
  //   compares athelete's expected speed to orignal and provides real time indications
endmodule

module speed___distance (
  input  [11:0] step_sec,
  input  [11:0] total_step,
  output [11:0] speed,
  output [11:0] distnace
);

  wire [11:0] divider_2_out, multiplier_2_out;
  wire [17:0] bit_extender_1_out, divider_1_out, multiplier_1_out;

  assign bit_extender_1_out = {{6{1'b0}}, total_step};  // Bit_Extender bit_extender_1
  Multiplier #(.width(18)) multiplier_1 (
    .a(bit_extender_1_out), .b(18'h4b), .out(multiplier_1_out));  // open: cin, cout
  Divider #(.width(18)) divider_1 (.a(multiplier_1_out), .b(18'h64), .out(divider_1_out));  // open: upper, rem
  Multiplier #(.width(12)) multiplier_2 (.a(12'h4b), .b(step_sec), .out(multiplier_2_out));  // open: cin, cout
  Bit_Extender #(.in_width(18), .out_width(12)) bit_extender_2 (.in(divider_1_out), .out(distnace));
  Divider #(.width(12)) divider_2 (.a(multiplier_2_out), .b(12'h32), .out(divider_2_out));  // open: upper, rem
  Adder #(.width(12)) adder_1 (.a(12'h2), .b(divider_2_out), .out(speed));  // open: cin, cout

  // Notes on the sheet:
  //   Speed and Distance calculator
endmodule

module timer (
  input  CLR,
  input  CLK,
  output out_3,
  output out_4,
  output out_5,
  output out_6,
  output out_7,
  output out_8,
  output out_9,
  output out_10,
  output out_11,
  output out_12,
  output out_13,
  output out_14,
  output out_15,
  output out_16,
  output out_17,
  output out_18,
  output out_19,
  output out_20,
  output out_21,
  output out_22,
  output out_23,
  output out_24,
  output out_25,
  output out_26
);

  wire and_1_out, and_2_out, and_3_out, and_4_out, and_5_out, and_6_out, and_7_out, and_8_out, and_9_out,
       and_10_out, not_1_out, not_2_out, not_3_out, not_4_out, not_5_out, not_6_out, not_7_out, not_8_out,
       not_9_out, not_10_out, not_11_out, not_12_out, not_13_out, not_14_out, or_1_out;

  and and_1 (and_1_out, not_1_out, not_2_out, out_5, not_3_out);
  and and_2 (and_2_out, and_1_out, and_4_out);
  not not_1 (not_1_out, out_3);
  not not_2 (not_2_out, out_4);
  mod_10_counter mod_10_counter_1 (
    .CLEAR(or_1_out), .CLK(and_3_out), .out_3(out_3), .out_4(out_4), .out_5(out_5), .out_6(out_6));
  and and_3 (and_3_out, out_10, not_4_out, not_5_out, out_7);
  not not_3 (not_3_out, out_6);
  and and_4 (and_4_out, not_6_out, out_8, not_7_out, not_8_out);
  not not_4 (not_4_out, out_9);
  not not_5 (not_5_out, out_8);
  not not_6 (not_6_out, out_7);
  and and_5 (and_5_out, and_7_out, and_6_out);
  mod_10_counter mod_10_counter_2 (
    .CLEAR(or_1_out), .CLK(and_5_out), .out_3(out_7), .out_4(out_8), .out_5(out_9), .out_6(out_10));
  and and_6 (and_6_out, out_14, not_9_out, out_12);
  not not_7 (not_7_out, out_9);
  not not_8 (not_8_out, out_10);
  mod_6_counter mod_6_counter_1 (.CLEAR(or_1_out), .CLK(and_7_out), .out_3(out_12), .out_4(out_13), .out_5(out_14));
  not not_9 (not_9_out, out_13);
  not not_10 (not_10_out, out_17);
  and and_7 (and_7_out, out_18, not_10_out, not_11_out, out_15);
  not not_11 (not_11_out, out_16);
  and and_8 (and_8_out, and_10_out, and_9_out);
  mod_10_counter mod_10_counter_3 (
    .CLEAR(or_1_out), .CLK(and_8_out), .out_3(out_15), .out_4(out_16), .out_5(out_17), .out_6(out_18));
  and and_9 (and_9_out, out_22, not_12_out, out_20);
  mod_6_counter mod_6_counter_2 (.CLEAR(or_1_out), .CLK(and_10_out), .out_3(out_20), .out_4(out_21), .out_5(out_22));
  not not_12 (not_12_out, out_21);
  not not_13 (not_13_out, out_25);
  and and_10 (and_10_out, out_26, not_13_out, not_14_out, out_23);
  not not_14 (not_14_out, out_24);
  or or_1 (or_1_out, CLR, and_2_out);
  mod_10_counter mod_10_counter_4 (
    .CLEAR(or_1_out), .CLK(CLK), .out_3(out_23), .out_4(out_24), .out_5(out_25), .out_6(out_26));

  assign out_11 = 1'b0;
  assign out_19 = 1'b0;

  // Notes on the sheet:
  //   TIMER
  //    sequential circuit used to generate time for stop watch 
endmodule

module timer_for_upperr_display (
  input  clear,
  input  clock,
  output [3:0] out_3,
  output [3:0] out_4,
  output [3:0] out_5,
  output [3:0] out_6,
  output [3:0] out_7,
  output [3:0] out_8
);

  wire bcd_to_seven_segment_decoder_1_c, bcd_to_seven_segment_decoder_1_out_8,
       bcd_to_seven_segment_decoder_1_out_9, bcd_to_seven_segment_decoder_2_c,
       bcd_to_seven_segment_decoder_2_out_8, bcd_to_seven_segment_decoder_2_out_9, timer_1_out_3,
       timer_1_out_4, timer_1_out_5, timer_1_out_6, timer_1_out_7, timer_1_out_8, timer_1_out_9,
       timer_1_out_10, timer_1_out_11, timer_1_out_12, timer_1_out_13, timer_1_out_14, timer_1_out_15,
       timer_1_out_16, timer_1_out_17, timer_1_out_18, timer_1_out_19, timer_1_out_20, timer_1_out_21,
       timer_1_out_22, timer_1_out_23, timer_1_out_24, timer_1_out_25, timer_1_out_26;

  bcd_to_seven_segment_decoder bcd_to_seven_segment_decoder_1 (
    .in_1(timer_1_out_3), .in_2(timer_1_out_4), .in_3(timer_1_out_5), .in_4(timer_1_out_6), .out_5(out_4[1]),
    .out_6(out_4[0]), .c(bcd_to_seven_segment_decoder_1_c), .out_8(bcd_to_seven_segment_decoder_1_out_8),
    .out_9(bcd_to_seven_segment_decoder_1_out_9), .out_10(out_4[2]), .out_11(out_4[3]));
  bcd_to_seven_segment_decoder bcd_to_seven_segment_decoder_2 (
    .in_1(timer_1_out_7), .in_2(timer_1_out_8), .in_3(timer_1_out_9), .in_4(timer_1_out_10),
    .out_5(out_5[1]), .out_6(out_5[0]), .c(bcd_to_seven_segment_decoder_2_c),
    .out_8(bcd_to_seven_segment_decoder_2_out_8), .out_9(bcd_to_seven_segment_decoder_2_out_9),
    .out_10(out_5[2]), .out_11(out_5[3]));
  bcd_to_seven_segment_decoder bcd_to_seven_segment_decoder_3 (
    .in_1(timer_1_out_11), .in_2(timer_1_out_12), .in_3(timer_1_out_13), .in_4(timer_1_out_14),
    .out_5(out_6[1]), .out_6(out_6[0]), .out_10(out_6[2]), .out_11(out_6[3]));  // open: c, out_8, out_9
  bcd_to_seven_segment_decoder bcd_to_seven_segment_decoder_4 (
    .in_1(timer_1_out_15), .in_2(timer_1_out_16), .in_3(timer_1_out_17), .in_4(timer_1_out_18),
    .out_5(out_7[1]), .out_6(out_7[0]), .out_10(out_7[2]), .out_11(out_7[3]));  // open: c, out_8, out_9
  timer timer_1 (
    .CLR(clear), .CLK(clock), .out_3(timer_1_out_3), .out_4(timer_1_out_4), .out_5(timer_1_out_5),
    .out_6(timer_1_out_6), .out_7(timer_1_out_7), .out_8(timer_1_out_8), .out_9(timer_1_out_9),
    .out_10(timer_1_out_10), .out_11(timer_1_out_11), .out_12(timer_1_out_12), .out_13(timer_1_out_13),
    .out_14(timer_1_out_14), .out_15(timer_1_out_15), .out_16(timer_1_out_16), .out_17(timer_1_out_17),
    .out_18(timer_1_out_18), .out_19(timer_1_out_19), .out_20(timer_1_out_20), .out_21(timer_1_out_21),
    .out_22(timer_1_out_22), .out_23(timer_1_out_23), .out_24(timer_1_out_24), .out_25(timer_1_out_25),
    .out_26(timer_1_out_26));
  bcd_to_seven_segment_decoder bcd_to_seven_segment_decoder_5 (
    .in_1(timer_1_out_19), .in_2(timer_1_out_20), .in_3(timer_1_out_21), .in_4(timer_1_out_22),
    .out_5(out_8[1]), .out_6(out_8[0]), .out_10(out_8[2]), .out_11(out_8[3]));  // open: c, out_8, out_9
  bcd_to_seven_segment_decoder bcd_to_seven_segment_decoder_6 (
    .in_1(timer_1_out_23), .in_2(timer_1_out_24), .in_3(timer_1_out_25), .in_4(timer_1_out_26),
    .out_5(out_3[1]), .out_6(out_3[0]), .out_10(out_3[2]), .out_11(out_3[3]));  // open: c, out_8, out_9

  // Notes on the sheet:
  //   COMPONENT OF STOPWATCH
endmodule

module timer_for_lower_display (
  input  clear,
  input  clock,
  output [3:0] out_3,
  output [3:0] out_4,
  output [3:0] out_5,
  output [3:0] out_6,
  output [3:0] out_7,
  output [3:0] out_8
);

  wire bcd_to_seven_segment_decoder_1_out_5, bcd_to_seven_segment_decoder_1_out_6,
       bcd_to_seven_segment_decoder_1_out_10, bcd_to_seven_segment_decoder_1_out_11,
       bcd_to_seven_segment_decoder_2_out_5, bcd_to_seven_segment_decoder_2_out_6,
       bcd_to_seven_segment_decoder_2_out_10, bcd_to_seven_segment_decoder_2_out_11;
  wire [23:0] timer_1_out_26;

  bcd_to_seven_segment_decoder bcd_to_seven_segment_decoder_1 (
    .in_1(timer_1_out_26[23]), .in_2(timer_1_out_26[22]), .in_3(timer_1_out_26[21]),
    .in_4(timer_1_out_26[20]), .out_5(bcd_to_seven_segment_decoder_1_out_5),
    .out_6(bcd_to_seven_segment_decoder_1_out_6), .c(out_4[1]), .out_8(out_4[2]), .out_9(out_4[3]),
    .out_10(bcd_to_seven_segment_decoder_1_out_10), .out_11(bcd_to_seven_segment_decoder_1_out_11));
  bcd_to_seven_segment_decoder bcd_to_seven_segment_decoder_2 (
    .in_1(timer_1_out_26[19]), .in_2(timer_1_out_26[18]), .in_3(timer_1_out_26[17]),
    .in_4(timer_1_out_26[16]), .out_5(bcd_to_seven_segment_decoder_2_out_5),
    .out_6(bcd_to_seven_segment_decoder_2_out_6), .c(out_5[1]), .out_8(out_5[2]), .out_9(out_5[3]),
    .out_10(bcd_to_seven_segment_decoder_2_out_10), .out_11(bcd_to_seven_segment_decoder_2_out_11));
  bcd_to_seven_segment_decoder bcd_to_seven_segment_decoder_3 (
    .in_1(timer_1_out_26[15]), .in_2(timer_1_out_26[14]), .in_3(timer_1_out_26[13]),
    .in_4(timer_1_out_26[12]), .c(out_6[1]), .out_8(out_6[2]), .out_9(out_6[3]));  // open: out_5, out_6, out_10, out_11
  bcd_to_seven_segment_decoder bcd_to_seven_segment_decoder_4 (
    .in_1(timer_1_out_26[11]), .in_2(timer_1_out_26[10]), .in_3(timer_1_out_26[9]), .in_4(timer_1_out_26[8]),
    .c(out_7[1]), .out_8(out_7[2]), .out_9(out_7[3]));  // open: out_5, out_6, out_10, out_11
  timer timer_1 (
    .CLR(clear), .CLK(clock), .out_3(timer_1_out_26[23]), .out_4(timer_1_out_26[22]),
    .out_5(timer_1_out_26[21]), .out_6(timer_1_out_26[20]), .out_7(timer_1_out_26[19]),
    .out_8(timer_1_out_26[18]), .out_9(timer_1_out_26[17]), .out_10(timer_1_out_26[16]),
    .out_11(timer_1_out_26[15]), .out_12(timer_1_out_26[14]), .out_13(timer_1_out_26[13]),
    .out_14(timer_1_out_26[12]), .out_15(timer_1_out_26[11]), .out_16(timer_1_out_26[10]),
    .out_17(timer_1_out_26[9]), .out_18(timer_1_out_26[8]), .out_19(timer_1_out_26[7]),
    .out_20(timer_1_out_26[6]), .out_21(timer_1_out_26[5]), .out_22(timer_1_out_26[4]),
    .out_23(timer_1_out_26[3]), .out_24(timer_1_out_26[2]), .out_25(timer_1_out_26[1]),
    .out_26(timer_1_out_26[0]));
  bcd_to_seven_segment_decoder bcd_to_seven_segment_decoder_5 (
    .in_1(timer_1_out_26[7]), .in_2(timer_1_out_26[6]), .in_3(timer_1_out_26[5]), .in_4(timer_1_out_26[4]),
    .c(out_8[1]), .out_8(out_8[2]), .out_9(out_8[3]));  // open: out_5, out_6, out_10, out_11
  bcd_to_seven_segment_decoder bcd_to_seven_segment_decoder_6 (
    .in_1(timer_1_out_26[3]), .in_2(timer_1_out_26[2]), .in_3(timer_1_out_26[1]), .in_4(timer_1_out_26[0]),
    .c(out_3[1]), .out_8(out_3[2]), .out_9(out_3[3]));  // open: out_5, out_6, out_10, out_11

  assign out_3[0] = 1'b1;
  assign out_4[0] = 1'b1;
  assign out_5[0] = 1'b1;
  assign out_6[0] = 1'b1;
  assign out_7[0] = 1'b1;
  assign out_8[0] = 1'b1;

  // Notes on the sheet:
  //   Component of Stop Watch
endmodule

module time_elapsed (
  input  clr,
  output [11:0] TIME_SECONDS
);

  wire clock_1_out;
  wire [3:0] timer_1_out_14, timer_1_out_18, timer_1_out_22, timer_1_out_26;
  wire [7:0] adder_1_out, adder_2_out, bit_extender_1_out, bit_extender_3_out, bit_extender_4_out,
       bit_extender_5_out, multiplier_1_out, multiplier_3_out;
  wire [11:0] bit_extender_2_out, bit_extender_6_out, multiplier_2_out;

  assign bit_extender_1_out = {{4{1'b0}}, timer_1_out_14};  // Bit_Extender bit_extender_1
  Multiplier multiplier_1 (.a(bit_extender_1_out), .b(8'ha), .out(multiplier_1_out));  // open: cin, cout
  assign bit_extender_2_out = {{4{1'b0}}, adder_1_out};  // Bit_Extender bit_extender_2
  assign bit_extender_3_out = {{4{1'b0}}, timer_1_out_18};  // Bit_Extender bit_extender_3
  Adder adder_1 (.a(bit_extender_3_out), .b(multiplier_1_out), .out(adder_1_out));  // open: cin, cout
  Multiplier #(.width(12)) multiplier_2 (
    .a(bit_extender_2_out), .b(12'h3c), .out(multiplier_2_out));  // open: cin, cout
  timer timer_1 (
    .CLR(clr), .CLK(clock_1_out), .out_11(timer_1_out_14[3]), .out_12(timer_1_out_14[2]),
    .out_13(timer_1_out_14[1]), .out_14(timer_1_out_14[0]), .out_15(timer_1_out_18[3]),
    .out_16(timer_1_out_18[2]), .out_17(timer_1_out_18[1]), .out_18(timer_1_out_18[0]),
    .out_19(timer_1_out_22[3]), .out_20(timer_1_out_22[2]), .out_21(timer_1_out_22[1]),
    .out_22(timer_1_out_22[0]), .out_23(timer_1_out_26[3]), .out_24(timer_1_out_26[2]),
    .out_25(timer_1_out_26[1]), .out_26(timer_1_out_26[0]));  // open: out_3, out_4, out_5, out_6, out_7, out_8, out_9, out_10
  assign bit_extender_4_out = {{4{1'b0}}, timer_1_out_26};  // Bit_Extender bit_extender_4
  assign bit_extender_5_out = {{4{1'b0}}, timer_1_out_22};  // Bit_Extender bit_extender_5
  Multiplier multiplier_3 (.a(bit_extender_5_out), .b(8'ha), .out(multiplier_3_out));  // open: cin, cout
  Clock clock_1 (.out(clock_1_out));
  Adder adder_2 (.a(bit_extender_4_out), .b(multiplier_3_out), .out(adder_2_out));  // open: cin, cout
  assign bit_extender_6_out = {{4{1'b0}}, adder_2_out};  // Bit_Extender bit_extender_6
  Adder #(.width(12)) adder_3 (.a(bit_extender_6_out), .b(multiplier_2_out), .out(TIME_SECONDS));  // open: cin, cout

  // Notes on the sheet:
  //   TIME ELAPSED (in seconds)
endmodule

module bcd0 (
  input  G,
  input  F,
  input  E,
  input  D,
  input  C,
  input  B,
  input  A,
  output w,
  output x,
  output y,
  output z
);

  wire and_1_out, and_2_out, and_3_out, and_4_out, and_5_out, and_6_out, and_7_out, and_8_out, and_9_out,
       and_10_out, and_11_out, and_12_out, and_13_out, nand_1_out, nand_2_out, nand_3_out, nand_4_out,
       nand_5_out, nand_6_out, nand_7_out, nand_8_out, nand_9_out, nand_10_out, nand_11_out, nand_12_out,
       nand_13_out, nand_14_out, nand_15_out, nand_16_out, nand_17_out, nand_18_out, nand_19_out,
       nand_20_out, nand_21_out, nand_22_out, nand_23_out, nand_24_out, nand_25_out, nand_26_out,
       nand_27_out, nand_28_out, nand_29_out, nand_30_out, nand_31_out, nand_32_out, nand_33_out,
       nand_34_out, nand_35_out, nand_36_out, nand_37_out, nand_38_out, nand_39_out, nand_40_out,
       nand_41_out, nand_42_out, nand_43_out, nand_44_out, nand_45_out, nand_46_out, nand_47_out,
       nand_48_out, nand_49_out, nand_50_out, nand_51_out, nand_52_out, nand_53_out, nand_54_out,
       nand_55_out, nand_56_out, nand_57_out, nand_58_out, nand_59_out, nand_60_out, nand_61_out,
       nand_62_out, nand_63_out, nand_64_out, nand_65_out, nand_66_out, nand_67_out, nand_68_out,
       nand_69_out, nand_70_out, nand_71_out, nand_72_out, nand_73_out, nand_74_out, nand_75_out,
       nand_76_out, nand_77_out, nand_78_out, nand_79_out, nand_80_out, nand_81_out, nand_82_out,
       nand_83_out, nand_84_out, nand_85_out, nand_86_out, nand_87_out, nand_88_out, nand_89_out,
       nand_90_out, nand_91_out, nand_92_out, nand_93_out, nand_94_out, nand_95_out, nand_96_out,
       nand_97_out, nand_98_out, nand_99_out, nand_100_out, nand_101_out, nand_102_out, not_1_out, not_2_out,
       not_3_out, not_4_out, not_5_out, not_6_out, not_7_out, not_8_out, not_9_out, not_10_out, not_11_out,
       not_12_out, not_13_out, not_14_out, not_15_out, not_16_out, not_17_out, not_18_out, not_19_out,
       not_20_out, not_21_out, not_22_out, not_23_out, not_24_out, not_25_out, not_26_out, not_27_out,
       not_28_out, not_29_out, not_30_out, not_31_out, not_32_out, not_33_out, not_34_out, not_35_out,
       not_36_out, not_37_out, not_38_out;

  nand nand_1 (nand_1_out, G, G);
  nand nand_2 (nand_2_out, F, F);
  nand nand_3 (nand_3_out, E, E);
  nand nand_4 (nand_4_out, C, C);
  nand nand_5 (nand_5_out, B, B);
  nand nand_6 (nand_6_out, G, G);
  nand nand_7 (nand_7_out, F, F);
  nand nand_8 (nand_8_out, D, D);
  nand nand_9 (nand_9_out, C, C);
  nand nand_10 (nand_10_out, G, G);
  nand nand_11 (nand_11_out, F, F);
  nand nand_12 (nand_12_out, B, B);
  nand nand_13 (nand_13_out, G, G);
  nand nand_14 (nand_14_out, E, E);
  nand nand_15 (nand_15_out, D, D);
  nand nand_16 (nand_16_out, G, G);
  nand nand_17 (nand_17_out, D, D);
  nand nand_18 (nand_18_out, C, C);
  nand nand_19 (nand_19_out, B, B);
  nand nand_20 (nand_20_out, G, G);
  nand nand_21 (nand_21_out, C, C);
  nand nand_22 (nand_22_out, F, F);
  nand nand_23 (nand_23_out, E, E);
  nand nand_24 (nand_24_out, D, D);
  nand nand_25 (nand_25_out, B, B);
  nand nand_26 (nand_26_out, F, F);
  nand nand_27 (nand_27_out, E, E);
  nand nand_28 (nand_28_out, F, F);
  nand nand_29 (nand_29_out, C, C);
  nand nand_30 (nand_30_out, B, B);
  nand nand_31 (nand_31_out, E, E);
  nand nand_32 (nand_32_out, D, D);
  nand nand_33 (nand_33_out, C, C);
  nand nand_34 (nand_34_out, G, G);
  nand nand_35 (nand_35_out, E, E);
  nand nand_36 (nand_36_out, D, D);
  nand nand_37 (nand_37_out, C, C);
  nand nand_38 (nand_38_out, G, G);
  nand nand_39 (nand_39_out, D, D);
  nand nand_40 (nand_40_out, F, F);
  nand nand_41 (nand_41_out, E, E);
  nand nand_42 (nand_42_out, B, B);
  not not_1 (not_1_out, F);
  not not_2 (not_2_out, E);
  not not_3 (not_3_out, D);
  not not_4 (not_4_out, C);
  not not_5 (not_5_out, G);
  not not_6 (not_6_out, F);
  not not_7 (not_7_out, D);
  not not_8 (not_8_out, F);
  not not_9 (not_9_out, E);
  not not_10 (not_10_out, B);
  not not_11 (not_11_out, G);
  not not_12 (not_12_out, F);
  not not_13 (not_13_out, D);
  not not_14 (not_14_out, C);
  not not_15 (not_15_out, B);
  not not_16 (not_16_out, G);
  not not_17 (not_17_out, F);
  not not_18 (not_18_out, C);
  not not_19 (not_19_out, E);
  not not_20 (not_20_out, D);
  not not_21 (not_21_out, C);
  not not_22 (not_22_out, B);
  not not_23 (not_23_out, G);
  not not_24 (not_24_out, D);
  not not_25 (not_25_out, B);
  not not_26 (not_26_out, G);
  not not_27 (not_27_out, E);
  not not_28 (not_28_out, G);
  not not_29 (not_29_out, G);
  not not_30 (not_30_out, C);
  not not_31 (not_31_out, B);
  not not_32 (not_32_out, F);
  not not_33 (not_33_out, E);
  not not_34 (not_34_out, B);
  not not_35 (not_35_out, F);
  not not_36 (not_36_out, B);
  not not_37 (not_37_out, F);
  not not_38 (not_38_out, D);
  nand nand_43 (nand_43_out, E, E);
  nand nand_44 (nand_44_out, D, D);
  nand nand_45 (nand_45_out, C, C);
  nand nand_46 (nand_46_out, G, G);
  nand nand_47 (nand_47_out, E, E);
  nand nand_48 (nand_48_out, D, D);
  nand nand_49 (nand_49_out, B, B);
  nand nand_50 (nand_50_out, G, G);
  nand nand_51 (nand_51_out, F, F);
  nand nand_52 (nand_52_out, E, E);
  nand nand_53 (nand_53_out, G, G);
  nand nand_54 (nand_54_out, F, F);
  nand nand_55 (nand_55_out, C, C);
  nand nand_56 (nand_56_out, B, B);
  nand nand_57 (nand_57_out, G, G);
  nand nand_58 (nand_58_out, F, F);
  nand nand_59 (nand_59_out, C, C);
  nand nand_60 (nand_60_out, G, G);
  nand nand_61 (nand_61_out, C, C);
  nand nand_62 (nand_62_out, B, B);
  nand nand_63 (nand_63_out, G, G);
  nand nand_64 (nand_64_out, E, E);
  nand nand_65 (nand_65_out, E, E);
  nand nand_66 (nand_66_out, D, D);
  nand nand_67 (nand_67_out, C, C);
  nand nand_68 (nand_68_out, B, B);
  nand nand_69 (nand_69_out, F, F);
  nand nand_70 (nand_70_out, E, E);
  nand nand_71 (nand_71_out, C, C);
  nand nand_72 (nand_72_out, F, F);
  nand nand_73 (nand_73_out, D, D);
  nand nand_74 (nand_74_out, F, F);
  and and_1 (and_1_out, not_1_out, not_2_out, not_3_out, not_4_out, B);
  and and_2 (and_2_out, not_5_out, not_6_out, not_7_out, C, B);
  and and_3 (and_3_out, not_8_out, not_9_out, D, C, not_10_out);
  and and_4 (and_4_out, not_11_out, not_12_out, E, not_13_out, not_14_out, not_15_out);
  and and_5 (and_5_out, not_16_out, not_17_out, E, D, not_18_out, B);
  and and_6 (and_6_out, F, not_19_out, not_20_out, not_21_out, not_22_out);
  and and_7 (and_7_out, not_23_out, F, not_24_out, C, not_25_out);
  and and_8 (and_8_out, not_26_out, F, not_27_out, D, B);
  and and_9 (and_9_out, not_28_out, F, D, C, B);
  and and_10 (and_10_out, not_29_out, F, E, D, not_30_out, not_31_out);
  and and_11 (and_11_out, G, not_32_out, not_33_out, D, not_34_out);
  and and_12 (and_12_out, G, not_35_out, D, C, not_36_out);
  and and_13 (and_13_out, G, not_37_out, E, not_38_out, B);
  nand nand_75 (nand_75_out, G, G);
  nand nand_76 (nand_76_out, F, F);
  nand nand_77 (nand_77_out, nand_1_out, nand_2_out, nand_3_out, D, nand_4_out, nand_5_out);
  nand nand_78 (nand_78_out, nand_6_out, nand_7_out, E, nand_8_out, nand_9_out, B);
  nand nand_79 (nand_79_out, nand_10_out, nand_11_out, E, D, C, nand_12_out);
  nand nand_80 (nand_80_out, nand_13_out, F, nand_14_out, nand_15_out, C, B);
  nand nand_81 (nand_81_out, nand_16_out, F, E, nand_17_out, nand_18_out, nand_19_out);
  nand nand_82 (nand_82_out, nand_20_out, F, E, D, nand_21_out, B);
  nand nand_83 (nand_83_out, G, nand_22_out, nand_23_out, nand_24_out, C, nand_25_out);
  nand nand_84 (nand_84_out, G, nand_26_out, nand_27_out, D, C, B);
  nand nand_85 (nand_85_out, G, nand_28_out, E, D, nand_29_out, nand_30_out);
  nand nand_86 (nand_86_out, G, F, nand_31_out, nand_32_out, nand_33_out, B);
  nand nand_87 (nand_87_out, nand_46_out, nand_47_out, nand_48_out, C, nand_49_out);
  nand nand_88 (nand_88_out, nand_50_out, nand_51_out, nand_52_out, C, B);
  nand nand_89 (nand_89_out, nand_53_out, nand_54_out, E, nand_55_out, nand_56_out);
  nand nand_90 (nand_90_out, nand_57_out, nand_58_out, E, D, nand_59_out);
  nand nand_91 (nand_91_out, nand_60_out, E, D, nand_61_out, nand_62_out);
  nand nand_92 (nand_92_out, nand_34_out, F, nand_35_out, nand_36_out, nand_37_out, B);
  nand nand_93 (nand_93_out, nand_63_out, F, nand_64_out, D, C);
  nand nand_94 (nand_94_out, nand_38_out, F, E, nand_39_out, C, B);
  nand nand_95 (nand_95_out, G, nand_65_out, nand_66_out, nand_67_out, nand_68_out);
  nand nand_96 (nand_96_out, G, nand_69_out, nand_70_out, nand_71_out, B);
  nand nand_97 (nand_97_out, G, nand_40_out, nand_41_out, D, C, nand_42_out);
  nand nand_98 (nand_98_out, G, nand_72_out, E, nand_73_out, C);
  nand nand_99 (nand_99_out, G, nand_74_out, E, C, B);
  nand nand_100 (nand_100_out, nand_75_out, A);
  nand nand_101 (nand_101_out, nand_76_out, A);
  nand nand_102 (nand_102_out, nand_43_out, nand_44_out, nand_45_out, A);
  nand nand_103 (w, nand_77_out, nand_78_out, nand_79_out, nand_80_out, nand_81_out, nand_82_out, nand_83_out, nand_84_out, nand_85_out, nand_86_out);
  nand nand_104 (x, nand_87_out, nand_88_out, nand_89_out, nand_90_out, nand_91_out, nand_92_out, nand_93_out, nand_94_out, nand_95_out, nand_96_out, nand_97_out, nand_98_out, nand_99_out);
  or or_1 (y, and_1_out, and_2_out, and_3_out, and_4_out, and_5_out, and_6_out, and_7_out, and_8_out, and_9_out, and_10_out, and_11_out, and_12_out, and_13_out);
  nand nand_105 (z, nand_100_out, nand_101_out, nand_102_out);

  // Notes on the sheet:
  //   7- BIT BINARY TO BCD CONVERTER
endmodule

module bcd1 (
  input  G,
  input  F,
  input  E,
  input  D,
  input  C,
  input  B,
  input  A,
  output s,
  output t,
  output u,
  output v
);

  wire nand_1_out, nand_2_out, nand_3_out, nand_4_out, nand_5_out, nand_6_out, nand_7_out, nand_8_out,
       nand_9_out, nand_10_out, nand_11_out, nand_12_out, nand_13_out, nand_14_out, nand_15_out, nand_16_out,
       nand_17_out, nand_18_out, nand_19_out, nand_20_out, nand_21_out, nand_22_out, nand_23_out,
       nand_24_out, nand_25_out, nand_26_out, nand_27_out, nand_28_out, nand_29_out, nand_30_out,
       nand_31_out, nand_32_out, nand_33_out, nand_34_out, nand_35_out, nand_36_out, nand_37_out,
       nand_38_out, nand_39_out, nand_40_out, nand_41_out, nand_42_out, nand_43_out, nand_44_out,
       nand_45_out, nand_46_out, nand_47_out, nand_48_out, nand_49_out, nand_50_out, nand_51_out,
       nand_52_out, nand_53_out, nand_54_out, nand_55_out, nand_56_out, nand_57_out, nand_58_out,
       nand_59_out, nand_60_out, nand_61_out, nand_62_out, nand_63_out, nand_64_out;

  nand nand_1 (nand_1_out, F, F);
  nand nand_2 (nand_2_out, E, E);
  nand nand_3 (nand_3_out, D, D);
  nand nand_4 (nand_4_out, C, C);
  nand nand_5 (nand_5_out, G, G);
  nand nand_6 (nand_6_out, G, G);
  nand nand_7 (nand_7_out, F, F);
  nand nand_8 (nand_8_out, E, E);
  nand nand_9 (nand_9_out, G, G);
  nand nand_10 (nand_10_out, F, F);
  nand nand_11 (nand_11_out, G, G);
  nand nand_12 (nand_12_out, F, F);
  nand nand_13 (nand_13_out, G, G);
  nand nand_14 (nand_14_out, G, G);
  nand nand_15 (nand_15_out, E, E);
  nand nand_16 (nand_16_out, D, D);
  nand nand_17 (nand_17_out, F, F);
  nand nand_18 (nand_18_out, E, E);
  nand nand_19 (nand_19_out, F, F);
  nand nand_20 (nand_20_out, E, E);
  nand nand_21 (nand_21_out, F, F);
  nand nand_22 (nand_22_out, E, E);
  nand nand_23 (nand_23_out, F, F);
  nand nand_24 (nand_24_out, G, G);
  nand nand_25 (nand_25_out, F, F);
  nand nand_26 (nand_26_out, D, D);
  nand nand_27 (nand_27_out, C, C);
  nand nand_28 (nand_28_out, E, E);
  nand nand_29 (nand_29_out, D, D);
  nand nand_30 (nand_30_out, C, C);
  nand nand_31 (nand_31_out, G, G);
  nand nand_32 (nand_32_out, D, D);
  nand nand_33 (nand_33_out, G, G);
  nand nand_34 (nand_34_out, D, D);
  nand nand_35 (nand_35_out, G, G);
  nand nand_36 (nand_36_out, C, C);
  nand nand_37 (nand_37_out, F, F);
  nand nand_38 (nand_38_out, E, E);
  nand nand_39 (nand_39_out, F, F);
  nand nand_40 (nand_40_out, E, E);
  nand nand_41 (nand_41_out, F, F);
  nand nand_42 (nand_42_out, F, F);
  nand nand_43 (nand_43_out, G, nand_1_out, E);
  nand nand_44 (nand_44_out, G, F, nand_2_out, nand_3_out, nand_4_out);
  nand nand_45 (nand_45_out, nand_5_out, F, D);
  nand nand_46 (nand_46_out, nand_6_out, F, E);
  nand nand_47 (nand_47_out, G, nand_7_out, nand_8_out);
  nand nand_48 (nand_48_out, nand_9_out, nand_10_out, E, C);
  nand nand_49 (nand_49_out, nand_11_out, nand_12_out, E, D);
  nand nand_50 (nand_50_out, nand_13_out, E, D, C);
  nand nand_51 (nand_51_out, nand_14_out, F, nand_15_out, nand_16_out);
  nand nand_52 (nand_52_out, G, nand_17_out, nand_18_out);
  nand nand_53 (nand_53_out, nand_19_out, nand_20_out, D, B);
  nand nand_54 (nand_54_out, nand_21_out, nand_22_out, D, C);
  nand nand_55 (nand_55_out, nand_23_out, D, C, B);
  nand nand_56 (nand_56_out, nand_24_out, nand_25_out, E, nand_26_out, nand_27_out);
  nand nand_57 (nand_57_out, F, nand_28_out, nand_29_out, nand_30_out);
  nand nand_58 (nand_58_out, nand_31_out, F, nand_32_out, B);
  nand nand_59 (nand_59_out, nand_33_out, F, nand_34_out, C);
  nand nand_60 (nand_60_out, nand_35_out, F, E, D, nand_36_out);
  nand nand_61 (nand_61_out, G, nand_37_out, nand_38_out, C, B);
  nand nand_62 (nand_62_out, G, nand_39_out, nand_40_out, D);
  nand nand_63 (nand_63_out, G, nand_41_out, D, B);
  nand nand_64 (nand_64_out, G, nand_42_out, D, C);
  nand nand_65 (s, nand_43_out, nand_44_out);
  nand nand_66 (t, nand_45_out, nand_46_out, nand_47_out);
  nand nand_67 (u, nand_48_out, nand_49_out, nand_50_out, nand_51_out, nand_52_out);
  nand nand_68 (v, nand_53_out, nand_54_out, nand_55_out, nand_56_out, nand_57_out, nand_58_out, nand_59_out, nand_60_out, nand_61_out, nand_62_out, nand_63_out, nand_64_out);

  // Notes on the sheet:
  //   7 BIT-BINARY TO BCD CONVERTER
endmodule

module _7seg_converter (
  input  A,
  input  B,
  input  C,
  input  D,
  output a_2,
  output b_2,
  output c_2,
  output d_2,
  output e,
  output f,
  output g
);

  wire and_1_out, and_2_out, and_3_out, and_4_out, and_5_out, and_6_out, and_7_out, and_8_out, and_9_out,
       and_10_out, and_11_out, and_12_out, and_13_out, and_14_out, and_15_out, and_16_out, not_1_out,
       not_2_out, not_3_out, not_4_out, not_5_out, not_6_out, not_7_out, not_8_out, not_9_out, not_10_out,
       not_11_out, not_12_out, not_13_out, not_14_out, not_15_out, not_16_out, not_17_out, not_18_out,
       not_19_out, not_20_out, not_21_out;

  not not_1 (not_1_out, B);
  not not_2 (not_2_out, D);
  not not_3 (not_3_out, C);
  not not_4 (not_4_out, D);
  not not_5 (not_5_out, C);
  not not_6 (not_6_out, B);
  not not_7 (not_7_out, D);
  not not_8 (not_8_out, B);
  not not_9 (not_9_out, D);
  not not_10 (not_10_out, C);
  not not_11 (not_11_out, B);
  not not_12 (not_12_out, D);
  not not_13 (not_13_out, D);
  not not_14 (not_14_out, C);
  not not_15 (not_15_out, D);
  not not_16 (not_16_out, C);
  not not_17 (not_17_out, D);
  not not_18 (not_18_out, B);
  not not_19 (not_19_out, C);
  not not_20 (not_20_out, D);
  and and_1 (and_1_out, not_1_out, not_2_out);
  and and_2 (and_2_out, B, D);
  not not_21 (not_21_out, B);
  and and_3 (and_3_out, not_3_out, not_4_out);
  and and_4 (and_4_out, C, D);
  or or_1 (c_2, not_5_out, D, B);
  and and_5 (and_5_out, not_6_out, not_7_out);
  and and_6 (and_6_out, not_8_out, C);
  and and_7 (and_7_out, C, not_9_out);
  and and_8 (and_8_out, B, not_10_out, D);
  and and_9 (and_9_out, not_11_out, not_12_out);
  and and_10 (and_10_out, C, not_13_out);
  and and_11 (and_11_out, not_14_out, not_15_out);
  and and_12 (and_12_out, B, not_16_out);
  and and_13 (and_13_out, B, not_17_out);
  and and_14 (and_14_out, not_18_out, C);
  and and_15 (and_15_out, B, not_19_out);
  and and_16 (and_16_out, B, not_20_out);
  or or_2 (a_2, and_1_out, C, and_2_out, A);
  or or_3 (b_2, not_21_out, and_3_out, and_4_out);
  or or_4 (d_2, and_5_out, and_6_out, and_7_out, and_8_out, A);
  or or_5 (e, and_9_out, and_10_out);
  or or_6 (f, and_11_out, and_12_out, and_13_out, A);
  or or_7 (g, and_14_out, and_15_out, and_16_out, A);

  // Notes on the sheet:
  //   BCD TO 7-SEGMENT DISPLAY
endmodule

module display_M (
  input  [11:0] val,
  output a1,
  output b1,
  output c1,
  output d1,
  output e1,
  output g1,
  output f1,
  output a,
  output b,
  output c,
  output d,
  output e,
  output g,
  output f
);

  wire LSB_w, LSB_x, LSB_y, LSB_z, MSB_s, MSB_t, MSB_u, MSB_v;
  wire [6:0] bit_extender_1_out;
  wire [11:0] divider_1_out;

  Divider #(.width(12)) divider_1 (.a(val), .b(12'h2), .out(divider_1_out));  // open: upper, rem
  Bit_Extender #(.in_width(12), .out_width(7)) bit_extender_1 (.in(divider_1_out), .out(bit_extender_1_out));
  bcd1 MSB (
    .G(bit_extender_1_out[6]), .F(bit_extender_1_out[5]), .E(bit_extender_1_out[4]),
    .D(bit_extender_1_out[3]), .C(bit_extender_1_out[2]), .B(bit_extender_1_out[1]),
    .A(bit_extender_1_out[0]), .s(MSB_s), .t(MSB_t), .u(MSB_u), .v(MSB_v));
  bcd0 LSB (
    .G(bit_extender_1_out[6]), .F(bit_extender_1_out[5]), .E(bit_extender_1_out[4]),
    .D(bit_extender_1_out[3]), .C(bit_extender_1_out[2]), .B(bit_extender_1_out[1]),
    .A(bit_extender_1_out[0]), .w(LSB_w), .x(LSB_x), .y(LSB_y), .z(LSB_z));
  _7seg_converter co_msb (
    .A(MSB_s), .B(MSB_t), .C(MSB_u), .D(MSB_v), .a_2(a1), .b_2(b1), .c_2(c1), .d_2(d1), .e(e1), .f(f1), .g(g1));
  _7seg_converter co_lsb (
    .A(LSB_w), .B(LSB_x), .C(LSB_y), .D(LSB_z), .a_2(a), .b_2(b), .c_2(c), .d_2(d), .e(e), .f(f), .g(g));

  // Notes on the sheet:
  //   7-segment display-1 
endmodule

module display_X (
  input  [11:0] val,
  output a1,
  output b1,
  output c1,
  output d1,
  output e1,
  output g1,
  output f1,
  output a,
  output b,
  output c,
  output d,
  output e,
  output g,
  output f
);

  wire LSB_w, LSB_x, LSB_y, LSB_z, MSB_s, MSB_t, MSB_u, MSB_v;
  wire [6:0] bit_extender_1_out;

  Bit_Extender #(.in_width(12), .out_width(7)) bit_extender_1 (.in(val), .out(bit_extender_1_out));
  bcd1 MSB (
    .G(bit_extender_1_out[6]), .F(bit_extender_1_out[5]), .E(bit_extender_1_out[4]),
    .D(bit_extender_1_out[3]), .C(bit_extender_1_out[2]), .B(bit_extender_1_out[1]),
    .A(bit_extender_1_out[0]), .s(MSB_s), .t(MSB_t), .u(MSB_u), .v(MSB_v));
  bcd0 LSB (
    .G(bit_extender_1_out[6]), .F(bit_extender_1_out[5]), .E(bit_extender_1_out[4]),
    .D(bit_extender_1_out[3]), .C(bit_extender_1_out[2]), .B(bit_extender_1_out[1]),
    .A(bit_extender_1_out[0]), .w(LSB_w), .x(LSB_x), .y(LSB_y), .z(LSB_z));
  _7seg_converter co_msb (
    .A(MSB_s), .B(MSB_t), .C(MSB_u), .D(MSB_v), .a_2(a1), .b_2(b1), .c_2(c1), .d_2(d1), .e(e1), .f(f1), .g(g1));
  _7seg_converter co_lsb (
    .A(LSB_w), .B(LSB_x), .C(LSB_y), .D(LSB_z), .a_2(a), .b_2(b), .c_2(c), .d_2(d), .e(e), .f(f), .g(g));

  // Notes on the sheet:
  //   7-segement display -2
endmodule

module bcd_to_seven_segment_decoder (
  input  in_1,
  input  in_2,
  input  in_3,
  input  in_4,
  output out_5,
  output out_6,
  output c,
  output out_8,
  output out_9,
  output out_10,
  output out_11
);

  wire decoder_1_out0, decoder_1_out1, decoder_1_out2, decoder_1_out3, decoder_1_out4, decoder_1_out5,
       decoder_1_out6, decoder_1_out7, decoder_1_out9;

  Decoder #(.select(4)) decoder_1 (
    .out0(decoder_1_out0), .out1(decoder_1_out1), .out2(decoder_1_out2), .out3(decoder_1_out3),
    .out4(decoder_1_out4), .out5(decoder_1_out5), .out6(decoder_1_out6), .out7(decoder_1_out7),
    .out9(decoder_1_out9), .sel({in_1, in_2, in_3, in_4}), .en(1'b1));  // open: out8, out10, out11, out12, out13, out14, out15
  or or_1 (out_5, decoder_1_out1, decoder_1_out4);
  or or_2 (out_6, decoder_1_out5, decoder_1_out6);
  or or_3 (c, decoder_1_out2, decoder_1_out2, decoder_1_out2);
  or or_4 (out_8, decoder_1_out1, decoder_1_out4, decoder_1_out7);
  or or_5 (out_9, decoder_1_out1, decoder_1_out3, decoder_1_out4, decoder_1_out5, decoder_1_out7, decoder_1_out9);
  or or_6 (out_10, decoder_1_out1, decoder_1_out2, decoder_1_out3, decoder_1_out7);
  or or_7 (out_11, decoder_1_out0, decoder_1_out1, decoder_1_out7);
  _7_Segment_Display #(.active("false")) u_7_segment_display_1 (
    .g(out_11), .f(out_10), .a(out_5), .b(out_6), .e(out_9), .d(out_8), .c(c), .dp(1'b1));

  // Notes on the sheet:
  //   BCD TO 7 SEGMENT DECODER
  //   a
  //   b
  //   d
  //   e
  //   f
  //   g
endmodule

module CLASSFICATION1 (
  input  [11:0] IN_HR,
  output [6:0] led1,
  output [6:0] led2,
  output [6:0] led2_2
);

  wire and_1_out, comparator_1_gt, comparator_1_lt, comparator_2_gt, comparator_2_lt;

  Comparator #(.width(12), .mode("unsigned")) comparator_1 (
    .a(IN_HR), .b(12'h96), .gt(comparator_1_gt), .lt(comparator_1_lt));  // open: eq
  Multiplexer #(.width(7)) multiplexer_1 (
    .in0({7{1'b0}}), .in1({7{1'b1}}), .out(led1), .sel(comparator_1_lt));  // open: en
  Comparator #(.width(12), .mode("unsigned")) comparator_2 (
    .a(IN_HR), .b(12'hfb4), .gt(comparator_2_gt), .lt(comparator_2_lt));  // open: eq
  Multiplexer #(.width(7)) multiplexer_2 (.in0({7{1'b0}}), .in1({7{1'b1}}), .out(led2), .sel(and_1_out));  // open: en
  and and_1 (and_1_out, comparator_2_lt, comparator_1_gt);
  Multiplexer #(.width(7)) multiplexer_3 (
    .in0({7{1'b0}}), .in1({7{1'b1}}), .out(led2_2), .sel(comparator_2_gt));  // open: en

  // Notes on the sheet:
  //   SAFETY CLASSIFIER
  //   <150 bpm
  //   150-180
  //   BPM
  //   >180 bpm
endmodule

module CLASSIFICATION2 (
  input  [11:0] IN_HR,
  output [6:0] led1,
  output [6:0] led2,
  output [6:0] led2_2
);

  wire and_1_out, comparator_1_gt, comparator_1_lt, comparator_2_gt, comparator_2_lt;

  Comparator #(.width(12), .mode("unsigned")) comparator_1 (
    .a(IN_HR), .b(12'h6e), .gt(comparator_1_gt), .lt(comparator_1_lt));  // open: eq
  Multiplexer #(.width(7)) multiplexer_1 (
    .in0({7{1'b0}}), .in1({7{1'b1}}), .out(led1), .sel(comparator_1_lt));  // open: en
  Comparator #(.width(12), .mode("unsigned")) comparator_2 (
    .a(IN_HR), .b(12'ha0), .gt(comparator_2_gt), .lt(comparator_2_lt));  // open: eq
  Multiplexer #(.width(7)) multiplexer_2 (.in0({7{1'b0}}), .in1({7{1'b1}}), .out(led2), .sel(and_1_out));  // open: en
  and and_1 (and_1_out, comparator_2_lt, comparator_1_gt);
  Multiplexer #(.width(7)) multiplexer_3 (
    .in0({7{1'b0}}), .in1({7{1'b1}}), .out(led2_2), .sel(comparator_2_gt));  // open: en

  // Notes on the sheet:
  //   WORKOUT INTENSITY CLASSIFIER
  //   <110 BPM
  //   110-160 BPM
  //   160 BPM
endmodule

module mod_10_counter (
  input  CLEAR,
  input  CLK,
  output out_3,
  output out_4,
  output out_5,
  output out_6
);

  wire and_1_out, and_2_out, and_3_out, and_4_out, j_k_ff_2_qn, j_k_ff_4_qn;

  and and_1 (and_1_out, out_6, out_5);
  and and_2 (and_2_out, j_k_ff_2_qn, out_6);
  J_K_Flip_Flop #(.trigger("falling")) j_k_ff_1 (
    .J(1'b1), .clk(CLK), .K(1'b1), .Q(out_6), .reset(CLEAR));  // open: Qn, preset, en
  J_K_Flip_Flop #(.trigger("falling")) j_k_ff_2 (
    .J(and_3_out), .clk(CLK), .K(and_1_out), .Q(out_5), .Qn(j_k_ff_2_qn), .reset(CLEAR));  // open: preset, en
  J_K_Flip_Flop #(.trigger("falling")) j_k_ff_3 (
    .J(and_1_out), .clk(CLK), .K(and_1_out), .Q(out_4), .reset(CLEAR));  // open: Qn, preset, en
  and and_3 (and_3_out, out_6, j_k_ff_4_qn);
  and and_4 (and_4_out, out_4, and_1_out);
  J_K_Flip_Flop #(.trigger("falling")) j_k_ff_4 (
    .J(and_4_out), .clk(CLK), .K(and_2_out), .Q(out_3), .Qn(j_k_ff_4_qn), .reset(CLEAR));  // open: preset, en

  // Notes on the sheet:
  //   d
  //   cd
  //   c'd
  //   MOD-10 COUNTER
  //   c
  //   a'd
  //   b
  //   bcd
  //   a
endmodule

module mod_6_counter (
  input  CLEAR,
  input  CLK,
  output out_3,
  output out_4,
  output out_5
);

  wire and_1_out, and_2_out, and_3_out, j_k_ff_2_qn, j_k_ff_3_qn;

  J_K_Flip_Flop #(.trigger("falling")) j_k_ff_1 (
    .J(1'b1), .clk(CLK), .K(1'b1), .Q(out_5), .reset(CLEAR));  // open: Qn, preset, en
  J_K_Flip_Flop #(.trigger("falling")) j_k_ff_2 (
    .J(and_1_out), .clk(CLK), .K(and_2_out), .Q(out_4), .Qn(j_k_ff_2_qn), .reset(CLEAR));  // open: preset, en
  and and_1 (and_1_out, j_k_ff_3_qn, out_5);
  and and_2 (and_2_out, out_4, out_5);
  and and_3 (and_3_out, j_k_ff_2_qn, out_5);
  J_K_Flip_Flop #(.trigger("falling")) j_k_ff_3 (
    .J(and_2_out), .clk(CLK), .K(and_3_out), .Q(out_3), .Qn(j_k_ff_3_qn), .reset(CLEAR));  // open: preset, en

  // Notes on the sheet:
  //   MOD-6 COUNTER
  //   c
  //   b
  //   a
endmodule

module HR_Generator2 (
  input  CLR,
  input  READY,
  output [7:0] out_3
);

  wire and_1_out, clock_1_out, clock_2_out, comparator_1_gt, comparator_2_gt, xor_1_out, xor_2_out;
  wire [7:0] _3_2_q;

  xor xor_1 (xor_1_out, _3_2_q[6], _3_2_q[3]);
  Clock clock_1 (.out(clock_1_out));
  D_Flip_Flop #(.trigger("falling")) _1 (
    .clk(clock_1_out), .D(xor_1_out), .Q(_3_2_q[7]), .preset(READY), .reset(CLR));  // open: Qn, en
  D_Flip_Flop #(.trigger("falling")) _2 (
    .clk(clock_1_out), .D(_3_2_q[7]), .Q(_3_2_q[4]), .reset(CLR));  // open: Qn, preset, en
  D_Flip_Flop #(.trigger("falling")) _3 (
    .clk(clock_1_out), .D(_3_2_q[4]), .Q(_3_2_q[6]), .reset(CLR));  // open: Qn, preset, en
  Comparator #(.mode("unsigned")) comparator_1 (.a(8'h64), .b(_3_2_q), .gt(comparator_1_gt));  // open: eq, lt
  D_Flip_Flop #(.trigger("falling")) _4 (
    .clk(clock_1_out), .D(_3_2_q[6]), .Q(_3_2_q[3]), .reset(CLR));  // open: Qn, preset, en
  Comparator #(.mode("unsigned")) comparator_2 (.a(8'hc3), .b(_3_2_q), .gt(comparator_2_gt));  // open: eq, lt
  xor xor_2 (xor_2_out, _3_2_q[0], _3_2_q[1]);
  Clock #(.highDuration(2), .lowDuration(2)) clock_2 (.out(clock_2_out));
  and and_1 (and_1_out, comparator_2_gt, comparator_1_gt);
  D_Flip_Flop #(.trigger("falling")) _1_2 (
    .clk(clock_2_out), .D(xor_2_out), .Q(_3_2_q[5]), .preset(READY), .reset(CLR));  // open: Qn, en
  Register register_1 (.D(_3_2_q), .Q(out_3), .clk(and_1_out));  // open: en, clr
  D_Flip_Flop #(.trigger("falling")) _2_2 (
    .clk(clock_2_out), .D(_3_2_q[5]), .Q(_3_2_q[2]), .reset(CLR));  // open: Qn, preset, en
  D_Flip_Flop #(.trigger("falling")) _3_2 (
    .clk(clock_2_out), .D(_3_2_q[2]), .Q(_3_2_q[0]), .reset(CLR));  // open: Qn, preset, en
  D_Flip_Flop #(.trigger("falling")) _4_2 (
    .clk(clock_2_out), .D(_3_2_q[0]), .Q(_3_2_q[1]), .reset(CLR));  // open: Qn, preset, en

  // Notes on the sheet:
  //   HR-GENERATOR(extra)
endmodule
